// Logisim project Assignment1.circ as structural Verilog
module Assignment2 (
  input  [11:0] Input_bits
);

  wire ALU0, ALU1, clock_1_out, D0, D1, Ma0, Ma1, Mb0, Mb1, R0, R1, R2, R3;
  wire [7:0] adder_1_out, and_1_out, demultiplexer_1_out0, demultiplexer_1_out1, demultiplexer_1_out2,
       demultiplexer_1_out3, multiplexer_1_out, multiplexer_2_out, multiplexer_3_out, or_1_out, R0_q, R1_q,
       R2_q, R3_q, subtractor_1_out;

  Clock clock_1 (.out(clock_1_out));
  Register u_R0 (.D(demultiplexer_1_out0), .en(R0), .clk(clock_1_out), .Q(R0_q));  // open: clr
  Register u_R1 (.D(demultiplexer_1_out1), .en(R1), .clk(clock_1_out), .Q(R1_q));  // open: clr
  Register u_R2 (.D(demultiplexer_1_out2), .en(R2), .clk(clock_1_out), .Q(R2_q));  // open: clr
  Register u_R3 (.D(demultiplexer_1_out3), .en(R3), .clk(clock_1_out), .Q(R3_q));  // open: clr
  Register #(.width(12)) Instructor_Register (
    .D(Input_bits), .clk(clock_1_out), .Q({R3, R2, R1, R0, Ma0, Ma1, Mb0, Mb1, ALU0, ALU1, D0, D1}));  // open: en, clr
  Multiplexer #(.enable("false"), .select(2), .width(8)) multiplexer_1 (
    .in0(R0_q), .in1(R1_q), .in2(R2_q), .in3(R3_q), .out(multiplexer_1_out), .sel({Ma1, Ma0}));
  Multiplexer #(.enable("false"), .select(2), .width(8)) multiplexer_2 (
    .in0(R0_q), .in1(R1_q), .in2(R2_q), .in3(R3_q), .out(multiplexer_2_out), .sel({Mb1, Mb0}));
  Adder adder_1 (.a(multiplexer_1_out), .b(multiplexer_2_out), .out(adder_1_out));  // open: cin, cout
  Subtractor subtractor_1 (.a(multiplexer_1_out), .b(multiplexer_2_out), .out(subtractor_1_out));  // open: bin, bout
  assign and_1_out = multiplexer_1_out & multiplexer_2_out;  // AND_Gate and_1, 8 bits wide
  assign or_1_out = multiplexer_1_out | multiplexer_2_out;  // OR_Gate or_1, 8 bits wide
  Multiplexer #(.enable("false"), .select(2), .width(8)) multiplexer_3 (
    .in0(adder_1_out), .in1(subtractor_1_out), .in2(and_1_out), .in3(or_1_out), .out(multiplexer_3_out),
    .sel({ALU1, ALU0}));
  Demultiplexer #(.enable("false"), .select(2), .width(8)) demultiplexer_1 (
    .out0(demultiplexer_1_out0), .out1(demultiplexer_1_out1), .out2(demultiplexer_1_out2),
    .out3(demultiplexer_1_out3), .in(multiplexer_3_out), .sel({D1, D0}));

  // Notes on the sheet:
  //   Clock and Enablers function 
  //   for register I/O operation
  //   Multiplexers's job is to select data from 
  //   specific registers to perform operations on
  //    Instructor Register is where program data is inputed 
  //   each bit has predefined selector function it tunnels into
  //   This part is considered the ALU
  //   Demultiplexer's job is assign on which Register to write the data
endmodule
