// Logisim project Assignment2.circ as structural Verilog
module Assignment2 (
  input  in_1,
  input  [20:0] in_2,
  input  [20:0] in_3
);

  wire ALU0, ALU1, clk, D0, D1, Ma0, Ma1, Mb0, Mb1, Mc0, R0, R1, R2, R3;
  wire [3:0] multiplexer_4_out, multiplexer_4_out_2;
  wire [7:0] adder_1_out, and_1_out, Counter_q, demultiplexer_1_out0, demultiplexer_1_out1,
       demultiplexer_1_out2, demultiplexer_1_out3, multiplexer_1_out, multiplexer_2_out, multiplexer_3_out,
       or_1_out, R0_q, R1_q, R2_q, R3_q, subtractor_1_out, V;

  Counter Counter (.Q(Counter_q), .clk(clk), .clr(in_1));  // open: load, D, count, carry
  Register u_R0 (.D(demultiplexer_1_out0), .en(R0), .clk(clk), .Q(R0_q));  // open: clr
  Register u_R1 (.D(demultiplexer_1_out1), .en(R1), .clk(clk), .Q(R1_q));  // open: clr
  Register u_R2 (.D(demultiplexer_1_out2), .en(R2), .clk(clk), .Q(R2_q));  // open: clr
  Register u_R3 (.D(demultiplexer_1_out3), .en(R3), .clk(clk), .Q(R3_q));  // open: clr
  ROM #(.dataWidth(21)) Memory (
    .addr(Counter_q), .data({Mc0, R3, R2, R1, R0, Ma1, Ma0, Mb1, Mb0, ALU1, ALU0, D1, D0, V}));
  Multiplexer #(.enable("false"), .select(2), .width(8)) multiplexer_1 (
    .in0(R0_q), .in1(R1_q), .in2(R2_q), .in3(R3_q), .out(multiplexer_1_out), .sel({Ma1, Ma0}));
  Multiplexer #(.enable("false"), .width(8)) multiplexer_2 (
    .in0(V), .in1(multiplexer_1_out), .out(multiplexer_2_out), .sel(Mc0));
  Multiplexer #(.enable("false"), .select(2), .width(8)) multiplexer_3 (
    .in0(R0_q), .in1(R1_q), .in2(R2_q), .in3(R3_q), .out(multiplexer_3_out), .sel({Mb1, Mb0}));
  Adder adder_1 (.a(multiplexer_2_out), .b(multiplexer_3_out), .out(adder_1_out));  // open: cin, cout
  Subtractor subtractor_1 (.a(multiplexer_2_out), .b(multiplexer_3_out), .out(subtractor_1_out));  // open: bin, bout
  assign and_1_out = multiplexer_2_out & multiplexer_3_out;  // AND_Gate and_1, 8 bits wide
  assign or_1_out = multiplexer_2_out | multiplexer_3_out;  // OR_Gate or_1, 8 bits wide
  Clock clock_1 (.out(clk));
  Hex_Digit_Display hex_digit_display_1 (.value(multiplexer_4_out_2));  // open: dp
  Multiplexer #(.enable("false"), .select(2), .width(8)) multiplexer_4 (
    .in0(adder_1_out), .in1(subtractor_1_out), .in2(and_1_out), .in3(or_1_out),
    .out({multiplexer_4_out_2, multiplexer_4_out}), .sel({ALU1, ALU0}));
  Demultiplexer #(.enable("false"), .select(2), .width(8)) demultiplexer_1 (
    .out0(demultiplexer_1_out0), .out1(demultiplexer_1_out1), .out2(demultiplexer_1_out2),
    .out3(demultiplexer_1_out3), .in({multiplexer_4_out_2, multiplexer_4_out}), .sel({D1, D0}));
  Hex_Digit_Display hex_digit_display_2 (.value(multiplexer_4_out));  // open: dp

  // Notes on the sheet:
  //   Reset Button
  //   to reset Counter
  //   Clock and Enablers function 
  //   for register I/O operation
  //   Counter to go through ROM data
  //   contents of Memory (hex, n*v repeats v):
  //   21900 5*21107
  //   Multiplexers's job is to select data from 
  //   specific registers to perform operations on
  //    Instructor Register is where program data is inputed 
  //   each bit has predefined selector function it tunnels into
  //   "Reset R1"
  //   "add 7 to R1"
  //   This part is considered the ALU
  //   Unfortunately, I did not know how to use the corresponding hexadecimal 
  //   values in ROM to output into binary 21 bits into instructor register :(
  //   -------------------------------------------------------
  //   0x 021900 = 00010 00 01 10 01 00000000 (ANDi R1, 0x00) "Reset R1"
  //   0x 021107 = 00010 00 01 00 01 00000111 (addi R1, 0x07) "add 7 to R1"
  //   second code repeated 5 times to accomplish 7 * 5 = 35 
  //   Demultiplexer's job is assign on which Register to write the data
endmodule
