// Logisim project update assiemnt2.circ as structural Verilog: 1 circuit, main circuit main
module main (
  input  in_1,
  input  in_2
);

  wire clk, clock_1_out, D1, D2, M0, M1, M2, M3, M4, M5, M6, R0, R1, R2, R3;
  wire [7:0] adder_1_out, and_1_out, counter_1_q, demultiplexer_1_out0, demultiplexer_1_out1,
       demultiplexer_1_out2, multiplexer_1_out, multiplexer_2_out, multiplexer_3_out, multiplexer_4_out,
       or_1_out, R0_q, register_1_q, register_2_q, register_3_q, subtractor_1_out, val;
  wire [20:0] rom_1_data;

  Counter counter_1 (.Q(counter_1_q), .clk(clock_1_out), .clr(in_2));  // open: load, D, count, carry
  Clock clock_1 (.out(clock_1_out));
  ROM #(.dataWidth(21)) rom_1 (.addr(counter_1_q), .data(rom_1_data));
  Register u_R0 (.D(demultiplexer_1_out0), .en(R0), .Q(R0_q), .clk(clk), .clr(clk));
  Register register_1 (.D(demultiplexer_1_out1), .en(R1), .Q(register_1_q), .clk(clk));  // open: clr
  Register register_2 (.D(demultiplexer_1_out0), .en(R3), .Q(register_2_q), .clk(clk));  // open: clr
  Register register_3 (.D(demultiplexer_1_out2), .en(R2), .Q(register_3_q), .clk(clk));  // open: clr
  Multiplexer #(.enable("false"), .select(2), .width(8)) multiplexer_1 (
    .in0(R0_q), .in1(register_1_q), .in2(register_3_q), .in3(register_2_q), .out(multiplexer_1_out),
    .sel({M0, M1}));
  Multiplexer #(.enable("false"), .select(2), .width(8)) multiplexer_2 (
    .in0(R0_q), .in1(register_1_q), .in2(register_3_q), .in3(register_2_q), .out(multiplexer_2_out),
    .sel({M2, M3}));
  Clock clock_2 (.out(clk));
  Multiplexer #(.enable("false"), .width(8)) multiplexer_3 (
    .in0(val), .in1(multiplexer_1_out), .out(multiplexer_3_out), .sel(M4));
  Adder adder_1 (.a(multiplexer_3_out), .b(multiplexer_2_out), .out(adder_1_out));  // open: cin, cout
  Subtractor subtractor_1 (.a(multiplexer_3_out), .b(multiplexer_2_out), .out(subtractor_1_out));  // open: bin, bout
  assign and_1_out = multiplexer_3_out & multiplexer_2_out;  // AND_Gate and_1, 8 bits wide
  assign or_1_out = multiplexer_3_out | multiplexer_2_out;  // OR_Gate or_1, 8 bits wide
  Register #(.width(21)) register_4 (
    .D(rom_1_data), .en(in_1), .Q({M4, R3, R2, R1, R0, M0, M1, M2, M3, M5, M6, D1, D2, val}), .clk(clk));  // open: clr
  Multiplexer #(.enable("false"), .select(2), .width(8)) multiplexer_4 (
    .in0(adder_1_out), .in1(subtractor_1_out), .in2(and_1_out), .in3(or_1_out), .out(multiplexer_4_out),
    .sel({M5, M6}));
  Demultiplexer #(.enable("false"), .select(2), .width(8)) demultiplexer_1 (
    .out0(demultiplexer_1_out0), .out1(demultiplexer_1_out1), .out2(demultiplexer_1_out2),
    .out3(demultiplexer_1_out0), .in(multiplexer_4_out), .sel({D1, D2}));

  // Notes on the sheet:
  //   contents of rom_1 (hex, n*v repeats v):
  //   21900 5*21107
endmodule
