// Logisim project Assignment3.circ as structural Verilog
module Assignment3 (
  input  in_1,
  input  [7:0] in_2,
  input  [7:0] in_3
);

  wire ALU0, ALU1, Beq, BeqN, clk, D0, D1, Jump, Ma0, Ma1, Mb0, Mb1, Mc0, nor_1_out, not_1_out, R0, R1, R2,
       R3, Sign;
  wire [6:0] V;
  wire [7:0] adder_1_out, adder_2_out, and_2_out, demultiplexer_1_out0, demultiplexer_1_out1,
       demultiplexer_1_out2, demultiplexer_1_out3, multiplexer_1_out, multiplexer_2_out, multiplexer_3_out,
       multiplexer_4_out, multiplexer_5_out, multiplexer_6_out, or_1_out, R0_q, R1_q, R2_q, R3_q,
       register_1_q, res, subtractor_1_out, subtractor_2_out;

  not not_1 (not_1_out, Beq);
  Multiplexer #(.enable("false"), .width(8)) multiplexer_1 (
    .in0({Sign, V}), .in1(in_2), .out(multiplexer_1_out), .sel(not_1_out));
  Register u_R0 (.D(demultiplexer_1_out0), .en(R0), .clk(clk), .Q(R0_q));  // open: clr
  Register u_R1 (.D(demultiplexer_1_out1), .en(R1), .clk(clk), .Q(R1_q));  // open: clr
  Register u_R2 (.D(demultiplexer_1_out2), .en(R2), .clk(clk), .Q(R2_q));  // open: clr
  Register u_R3 (.D(demultiplexer_1_out3), .en(R3), .clk(clk), .Q(R3_q));  // open: clr
  Adder adder_1 (.a(register_1_q), .b(multiplexer_1_out), .out(adder_1_out));  // open: cin, cout
  Subtractor subtractor_1 (.a(register_1_q), .b(multiplexer_1_out), .out(subtractor_1_out));  // open: bin, bout
  nor nor_1 (nor_1_out, in_3[0], in_3[1], in_3[2], in_3[3], in_3[4], in_3[5], in_3[6], in_3[7], res[0], res[1], res[2], res[3], res[4], res[5], res[6], res[7]);
  Multiplexer #(.enable("false"), .width(8)) multiplexer_2 (
    .in0(adder_1_out), .in1(subtractor_1_out), .out(multiplexer_2_out), .sel(Sign));
  Multiplexer #(.enable("false"), .select(2), .width(8)) multiplexer_3 (
    .in0(R0_q), .in1(R1_q), .in2(R2_q), .in3(R3_q), .out(multiplexer_3_out), .sel({Ma1, Ma0}));
  Multiplexer #(.enable("false"), .width(8)) multiplexer_4 (
    .in0({Sign, V}), .in1(multiplexer_2_out), .out(multiplexer_4_out), .sel(Jump));
  Multiplexer #(.enable("false"), .width(8)) multiplexer_5 (
    .in0({Sign, V}), .in1(multiplexer_3_out), .out(multiplexer_5_out), .sel(Mc0));
  Multiplexer #(.enable("false"), .select(2), .width(8)) multiplexer_6 (
    .in0(R0_q), .in1(R1_q), .in2(R2_q), .in3(R3_q), .out(multiplexer_6_out), .sel({Mb1, Mb0}));
  Register register_1 (.D(multiplexer_4_out), .en(in_1), .clk(clk), .Q(register_1_q));  // open: clr
  Clock clock_1 (.out(clk));
  and and_1 (Beq, BeqN, nor_1_out);
  Adder adder_2 (.a(multiplexer_5_out), .b(multiplexer_6_out), .out(adder_2_out));  // open: cin, cout
  Subtractor subtractor_2 (.a(multiplexer_5_out), .b(multiplexer_6_out), .out(subtractor_2_out));  // open: bin, bout
  assign and_2_out = multiplexer_5_out & multiplexer_6_out;  // AND_Gate and_2, 8 bits wide
  assign or_1_out = multiplexer_5_out | multiplexer_6_out;  // OR_Gate or_1, 8 bits wide
  ROM #(.dataWidth(23)) Memory (
    .addr(register_1_q),
    .data({BeqN, Jump, Mc0, R3, R2, R1, R0, Ma1, Ma0, Mb1, Mb0, ALU1, ALU0, D1, D0, Sign, V}));
  Hex_Digit_Display hex_digit_display_1 (.value(res[7:4]));  // open: dp
  Multiplexer #(.enable("false"), .select(2), .width(8)) multiplexer_7 (
    .in0(adder_2_out), .in1(subtractor_2_out), .in2(and_2_out), .in3(or_1_out), .out(res), .sel({ALU1, ALU0}));
  Demultiplexer #(.enable("false"), .select(2), .width(8)) demultiplexer_1 (
    .out0(demultiplexer_1_out0), .out1(demultiplexer_1_out1), .out2(demultiplexer_1_out2),
    .out3(demultiplexer_1_out3), .in(res), .sel({D1, D0}));
  Hex_Digit_Display hex_digit_display_2 (.value(res[3:0]));  // open: dp

  // Other names for the same wires on the sheet: V[7] = Sign

  // Notes on the sheet:
  //   branch dependent value
  //   Rx - Ry
  //   Relative Jumping address, 
  //   an 8 bit signed number
  //   Selector for relative jump, 
  //   otherwise just count + 1
  //   Clock and Enablers function 
  //   for register I/O operation
  //   Absolute Jumping address
  //   Multiplexers's job is to select data from 
  //   specific registers to perform operations on
  //   NOR'ing the result of Rx - Ry for example, 
  //   only works the dependent value of branching 
  //   Register to store functions as current 
  //   state for our make shift counter
  //   Demultiplexer's job is assign on which Register to write the data
  //   This part is considered the ALU
  //   contents of Memory (hex, n*v repeats v):
  //   21900 5*21107
  //   Was not able to formulate a functioning instruction set to loop through 5 * 7 :(
endmodule
