// Logisim project Assignment4.circ as structural Verilog
module Assignment4 (
  input  in_1,
  input  in_2,
  input  [7:0] in_3
);

  wire ALU0, ALU1, Beq, BeqN, button_1_out, clk, comparator_1_eq, D0, D1, Jump, Ma0, Ma1, Mb0, Mb1, Mc0, neg,
       not_1_out, not_2_out, not_4_out, not_5_out, or_1_out, R0, R1, R2, R3, Sign;
  wire [7:0] adder_1_out, adder_2_out, and_2_out, demultiplexer_1_out0, demultiplexer_1_out1,
       demultiplexer_1_out2, demultiplexer_1_out3, Div, multiplexer_2_out, multiplexer_3_out,
       multiplexer_4_out, multiplexer_5_out, multiplexer_6_out, multiplexer_7_out, multiplexer_8_out,
       negator_1_out, or_2_out, R0b, R1_q, register_1_q, Rem, res, subtractor_1_out, subtractor_2_out, V;

  Multiplexer #(.enable("false")) multiplexer_1 (.in0(V[7]), .in1(in_2), .out(Sign), .sel(not_1_out));
  not not_1 (not_1_out, Beq);
  not not_2 (not_2_out, Beq);
  Multiplexer #(.enable("false"), .width(8)) multiplexer_2 (
    .in0({in_2, V[6:0]}), .in1(in_3), .out(multiplexer_2_out), .sel(not_2_out));
  Register u_R0 (.D(demultiplexer_1_out0), .en(R0), .clk(clk), .Q(R0b));  // open: clr
  Register u_R1 (.D(demultiplexer_1_out1), .en(R1), .clk(clk), .Q(R1_q));  // open: clr
  Register u_R2 (.D(demultiplexer_1_out2), .en(R2), .clk(clk), .Q(Rem));  // open: clr
  Register u_R3 (.D(demultiplexer_1_out3), .en(R3), .clk(clk), .Q(Div));  // open: clr
  Adder adder_1 (.a(register_1_q), .b(multiplexer_2_out), .out(adder_1_out));  // open: cin, cout
  Subtractor subtractor_1 (.a(register_1_q), .b(multiplexer_2_out), .out(subtractor_1_out));  // open: bin, bout
  or or_1 (or_1_out, R0b[0], R0b[1], R0b[2], R0b[3], R0b[4], R0b[5], R0b[6], R0b[7], res[0], res[1], res[2], res[3], res[4], res[5], res[6], res[7]);
  // NOT_Gate not_3 has open pins: in=or_1_out, out=open
  Multiplexer #(.enable("false"), .select(2), .width(8)) multiplexer_3 (
    .in0(R0b), .in1(R1_q), .in2(Rem), .in3(Div), .out(multiplexer_3_out), .sel({Ma1, Ma0}));
  Multiplexer #(.enable("false"), .width(8)) multiplexer_4 (
    .in0(adder_1_out), .in1(subtractor_1_out), .out(multiplexer_4_out), .sel(Sign));
  not not_4 (not_4_out, Jump);
  Comparator comparator_1 (.a(R0b), .b(res), .eq(comparator_1_eq));  // open: gt, lt
  Multiplexer #(.enable("false"), .width(8)) multiplexer_5 (
    .in0(V), .in1(multiplexer_3_out), .out(multiplexer_5_out), .sel(not_5_out));
  not not_5 (not_5_out, Mc0);
  Multiplexer #(.enable("false"), .select(2), .width(8)) multiplexer_6 (
    .in0(R0b), .in1(R1_q), .in2(Rem), .in3(Div), .out(multiplexer_6_out), .sel({Mb1, Mb0}));
  Multiplexer #(.enable("false"), .width(8)) multiplexer_7 (
    .in0(V), .in1(multiplexer_4_out), .out(multiplexer_7_out), .sel(not_4_out));
  Subtractor subtractor_2 (.a(multiplexer_5_out), .b(multiplexer_6_out), .out(subtractor_2_out));  // open: bin, bout
  Register register_1 (.D(multiplexer_7_out), .en(in_1), .clk(clk), .Q(register_1_q), .clr(button_1_out));
  Clock clock_1 (.out(clk));
  and and_1 (Beq, BeqN, comparator_1_eq);
  Adder adder_2 (.a(multiplexer_5_out), .b(multiplexer_6_out), .out(adder_2_out));  // open: cin, cout
  Negator negator_1 (.in(subtractor_2_out), .out(negator_1_out));
  assign and_2_out = multiplexer_5_out & multiplexer_6_out;  // AND_Gate and_2, 8 bits wide
  assign or_2_out = multiplexer_5_out | multiplexer_6_out;  // OR_Gate or_2, 8 bits wide
  Button button_1 (.out(button_1_out));
  Multiplexer #(.enable("false"), .width(8)) multiplexer_8 (
    .in0(subtractor_2_out), .in1(negator_1_out), .out(multiplexer_8_out), .sel(neg));
  Hex_Digit_Display hex_digit_display_1 (.value(res[7:4]));  // open: dp
  Multiplexer #(.enable("false"), .select(2), .width(8)) multiplexer_9 (
    .in0(adder_2_out), .in1(multiplexer_8_out), .in2(and_2_out), .in3(or_2_out), .out(res), .sel({ALU1, ALU0}));
  Demultiplexer #(.enable("false"), .select(2), .width(8)) demultiplexer_1 (
    .out0(demultiplexer_1_out0), .out1(demultiplexer_1_out1), .out2(demultiplexer_1_out2),
    .out3(demultiplexer_1_out3), .in(res), .sel({D1, D0}));
  ROM #(.dataWidth(24)) Memory (
    .addr(register_1_q),
    .data({neg, BeqN, Jump, Mc0, R3, R2, R1, R0, Ma1, Ma0, Mb1, Mb0, ALU1, ALU0, D1, D0, V}));
  Hex_Digit_Display hex_digit_display_2 (.value(res[3:0]));  // open: dp
  Hex_Digit_Display hex_digit_display_3 (.value(Div[7:4]));  // open: dp
  Hex_Digit_Display hex_digit_display_4 (.value(Rem[7:4]));  // open: dp
  Hex_Digit_Display hex_digit_display_5 (.value(Div[3:0]));  // open: dp
  Hex_Digit_Display hex_digit_display_6 (.value(Rem[3:0]));  // open: dp

  // Notes on the sheet:
  //   Selector for relative jump, 
  //   otherwise just count + 1
  //   Rx - Ry
  //   Clock and Enablers function 
  //   for register I/O operation
  //   Relative Jumping address, 
  //   an 8 bit signed number
  //   Multiplexers's job is to select data from 
  //   specific registers to perform operations on
  //   Absolute Jumping address
  //   AND
  //   OR
  //   Reset Button
  //   Register to store functions as current 
  //   state for our make shift counter
  //   Demultiplexer's job is assign on which Register to write the data
  //   This part is considered the ALU
  //   contents of Memory (hex, n*v repeats v):
  //   10800 20900 40a00 83b00 121179 14220c 26500 183301 942601 406403 408482 400485
  //   1 - ANDi, R0, 0x00, R0
  //   2 - ANDi, R1, 0x00, R1
  //   3 - ANDi, R2, 0x00, R2
  //   4 - ANDi, R3, 0x00, R3
  //   -----------
  //   5 - addi, R1, 0x79, R1 
  //   6 - addi, R2, 0x0c, R2
  //   ------------
  //   7 - sub, R1,  R2  , R1
  //   8 - addi, R3, 0x01, R3
  //   9 - subi, R2, 0x01, R2
  //   --------------
  //   10 - BeqN, R1, R2, 0x0d
  //   11 - BeqN, R2, R0, 0x82
  //   12 - BeqN, R0, R0, 0x85
  //   Psuedo code
  //   Initializing
  //   Operations
  //   Division Result
  //   Remainder
  //   Clear Memory
  //    Jump to address 13 "Break out"
  //   Jump to address 9 
  //   Jump to address 6
endmodule
