// Logisim project assignment8_Hayan.circ as structural Verilog: 4 circuits, main circuit main1
module main1 (
  input  [1:0] ShiftOp,
  input  [1:0] ALUselector,
  input  ArithOp,
  input  [1:0] LogicOp
);

  wire adder_1_cout, Clk, EnabelW, Zero;
  wire [4:0] RA, RB, RW;
  wire [31:0] adder_1_out, and_1_out, bit_extender_1_out, multiplexer_1_out, multiplexer_2_out, nor_1_out,
       or_1_out, Registers_busa, Registers_busb, Shitfer_data_out, SLT_data_out, xor_1_out, xor_2_out;

  Clock clock_1 (.out(Clk));
  Regisiters Registers (
    .Clk(Clk), .RA(RA), .RB(RB), .BusW(multiplexer_2_out), .EnableWrite(EnabelW), .RW(RW),
    .BusA(Registers_busa), .BusB(Registers_busb));
  assign and_1_out = Registers_busa & Registers_busb;  // AND_Gate and_1, 32 bits wide
  assign or_1_out = Registers_busa | Registers_busb;  // OR_Gate or_1, 32 bits wide
  assign nor_1_out = ~(Registers_busa | Registers_busb);  // NOR_Gate nor_1, 32 bits wide
  assign xor_1_out = Registers_busa ^ Registers_busb;  // XOR_Gate xor_1, 32 bits wide
  assign bit_extender_1_out = {{31{ArithOp}}, ArithOp};  // Bit_Extender bit_extender_1
  assign xor_2_out = Registers_busb ^ bit_extender_1_out;  // XOR_Gate xor_2, 32 bits wide
  Multiplexer #(.select(2), .width(32)) multiplexer_1 (
    .in0(and_1_out), .in1(or_1_out), .in2(nor_1_out), .in3(xor_1_out), .out(multiplexer_1_out), .sel(LogicOp));
  Adder #(.width(32)) adder_1 (
    .a(Registers_busa), .b(xor_2_out), .out(adder_1_out), .cin(ArithOp), .cout(adder_1_cout));
  Shifter Shitfer (
    .ShiftVal(Registers_busa[4:0]), .Data(Registers_busb), .ShiftOp(ShiftOp), .Data_Out(Shitfer_data_out));
  Sign SLT (.Data(adder_1_out[31]), .Overflow(adder_1_cout), .Data_Out(SLT_data_out));
  Multiplexer #(.select(2), .width(32)) multiplexer_2 (
    .in0(Shitfer_data_out), .in1(SLT_data_out), .in2(adder_1_out), .in3(multiplexer_1_out),
    .out(multiplexer_2_out), .sel(ALUselector));
  nor nor_2 (Zero, multiplexer_2_out[16], multiplexer_2_out[31], multiplexer_2_out[30], multiplexer_2_out[29], multiplexer_2_out[28], multiplexer_2_out[27], multiplexer_2_out[26], multiplexer_2_out[25], multiplexer_2_out[24], multiplexer_2_out[23], multiplexer_2_out[22], multiplexer_2_out[21], multiplexer_2_out[20], multiplexer_2_out[19], multiplexer_2_out[18], multiplexer_2_out[17], multiplexer_2_out[15], multiplexer_2_out[14], multiplexer_2_out[13], multiplexer_2_out[12], multiplexer_2_out[11], multiplexer_2_out[10], multiplexer_2_out[9], multiplexer_2_out[8], multiplexer_2_out[7], multiplexer_2_out[6], multiplexer_2_out[5], multiplexer_2_out[4], multiplexer_2_out[3], multiplexer_2_out[2], multiplexer_2_out[1], multiplexer_2_out[0]);

  // Notes on the sheet:
  //   BusW
  //   SLL = 00
  //   SRL = 01
  //   BusA
  //   BusB
  //   SRA = 10
  //   ROR = 11
  //   ADD = 0
  //   SUB = 1
  //   Logic
  //   ALU
  //   AND = 00
  //   OR = 01
  //   NOR = 10
  //   XOR = 11
  //    !=
  //   Shift = 00
  //   SLT = 01
  //   Arith = 10
  //   Logic = 11
endmodule

module Regisiters (
  input  Clk,
  input  [4:0] RA,
  input  [4:0] RB,
  input  [31:0] BusW,
  input  EnableWrite,
  input  [4:0] RW,
  output [31:0] BusA,
  output [31:0] BusB
);

  wire and_1_out, and_2_out, and_3_out, and_4_out, and_5_out, and_6_out, and_7_out, and_8_out, and_9_out,
       and_10_out, and_11_out, and_12_out, and_13_out, and_14_out, and_15_out, and_16_out, and_17_out,
       and_18_out, and_19_out, and_20_out, and_21_out, and_22_out, and_23_out, and_24_out, and_25_out,
       and_26_out, and_27_out, and_28_out, and_29_out, and_30_out, and_31_out, decoder_1_out1,
       decoder_1_out2, decoder_1_out3, decoder_1_out4, decoder_1_out5, decoder_1_out6, decoder_1_out7,
       decoder_1_out8, decoder_1_out9, decoder_1_out10, decoder_1_out11, decoder_1_out12, decoder_1_out13,
       decoder_1_out14, decoder_1_out15, decoder_1_out16, decoder_1_out17, decoder_1_out18, decoder_1_out19,
       decoder_1_out20, decoder_1_out21, decoder_1_out22, decoder_1_out23, decoder_1_out24, decoder_1_out25,
       decoder_1_out26, decoder_1_out27, decoder_1_out28, decoder_1_out29, decoder_1_out30, decoder_1_out31,
       decoder_2_out0, decoder_2_out1, decoder_2_out2, decoder_2_out3, decoder_2_out4, decoder_2_out5,
       decoder_2_out6, decoder_2_out7, decoder_2_out8, decoder_2_out9, decoder_2_out10, decoder_2_out11,
       decoder_2_out12, decoder_2_out13, decoder_2_out14, decoder_2_out15, decoder_2_out16, decoder_2_out17,
       decoder_2_out18, decoder_2_out19, decoder_2_out20, decoder_2_out21, decoder_2_out22, decoder_2_out23,
       decoder_2_out24, decoder_2_out25, decoder_2_out26, decoder_2_out27, decoder_2_out28, decoder_2_out29,
       decoder_2_out30, decoder_2_out31, decoder_3_out0, decoder_3_out1, decoder_3_out2, decoder_3_out3,
       decoder_3_out4, decoder_3_out5, decoder_3_out6, decoder_3_out7, decoder_3_out8, decoder_3_out9,
       decoder_3_out10, decoder_3_out11, decoder_3_out12, decoder_3_out13, decoder_3_out14, decoder_3_out15,
       decoder_3_out16, decoder_3_out17, decoder_3_out18, decoder_3_out19, decoder_3_out20, decoder_3_out21,
       decoder_3_out22, decoder_3_out23, decoder_3_out24, decoder_3_out25, decoder_3_out26, decoder_3_out27,
       decoder_3_out28, decoder_3_out29, decoder_3_out30, decoder_3_out31;
  wire [31:0] R0_q, R1_q, R2_q, R3_q, R4_q, R5_q, R6_q, R7_q, R8_q, R9_q, R10_q, R11_q, R12_q, R13_q, R14_q,
       R15_q, R18_q, R19_q, R20_q, R21_q, R22_q, R23_q, R24_q, R25_q, R26_q, R27_q, R28_q, R29_q, R30_q,
       R31_q, undriven, undriven_2;

  Decoder #(.enable("false"), .select(5)) decoder_1 (
    .out1(decoder_1_out1), .out2(decoder_1_out2), .out3(decoder_1_out3), .out4(decoder_1_out4),
    .out5(decoder_1_out5), .out6(decoder_1_out6), .out7(decoder_1_out7), .out8(decoder_1_out8),
    .out9(decoder_1_out9), .out10(decoder_1_out10), .out11(decoder_1_out11), .out12(decoder_1_out12),
    .out13(decoder_1_out13), .out14(decoder_1_out14), .out15(decoder_1_out15), .out16(decoder_1_out16),
    .out17(decoder_1_out17), .out18(decoder_1_out18), .out19(decoder_1_out19), .out20(decoder_1_out20),
    .out21(decoder_1_out21), .out22(decoder_1_out22), .out23(decoder_1_out23), .out24(decoder_1_out24),
    .out25(decoder_1_out25), .out26(decoder_1_out26), .out27(decoder_1_out27), .out28(decoder_1_out28),
    .out29(decoder_1_out29), .out30(decoder_1_out30), .out31(decoder_1_out31), .sel(RW));  // open: out0
  and and_1 (and_1_out, EnableWrite, decoder_1_out1);
  and and_2 (and_2_out, EnableWrite, decoder_1_out2);
  and and_3 (and_3_out, EnableWrite, decoder_1_out3);
  and and_4 (and_4_out, EnableWrite, decoder_1_out4);
  and and_5 (and_5_out, EnableWrite, decoder_1_out5);
  and and_6 (and_6_out, EnableWrite, decoder_1_out6);
  and and_7 (and_7_out, EnableWrite, decoder_1_out7);
  and and_8 (and_8_out, EnableWrite, decoder_1_out8);
  and and_9 (and_9_out, EnableWrite, decoder_1_out9);
  and and_10 (and_10_out, EnableWrite, decoder_1_out10);
  and and_11 (and_11_out, EnableWrite, decoder_1_out11);
  and and_12 (and_12_out, EnableWrite, decoder_1_out12);
  and and_13 (and_13_out, EnableWrite, decoder_1_out13);
  and and_14 (and_14_out, EnableWrite, decoder_1_out14);
  and and_15 (and_15_out, EnableWrite, decoder_1_out15);
  and and_16 (and_16_out, EnableWrite, decoder_1_out16);
  and and_17 (and_17_out, EnableWrite, decoder_1_out17);
  and and_18 (and_18_out, EnableWrite, decoder_1_out18);
  and and_19 (and_19_out, EnableWrite, decoder_1_out19);
  and and_20 (and_20_out, EnableWrite, decoder_1_out20);
  and and_21 (and_21_out, EnableWrite, decoder_1_out21);
  and and_22 (and_22_out, EnableWrite, decoder_1_out22);
  and and_23 (and_23_out, EnableWrite, decoder_1_out23);
  and and_24 (and_24_out, EnableWrite, decoder_1_out24);
  and and_25 (and_25_out, EnableWrite, decoder_1_out25);
  and and_26 (and_26_out, EnableWrite, decoder_1_out26);
  and and_27 (and_27_out, EnableWrite, decoder_1_out27);
  and and_28 (and_28_out, EnableWrite, decoder_1_out28);
  and and_29 (and_29_out, EnableWrite, decoder_1_out29);
  and and_30 (and_30_out, EnableWrite, decoder_1_out30);
  and and_31 (and_31_out, EnableWrite, decoder_1_out31);
  Register #(.width(32)) R0 (.D({32{1'b0}}), .en(1'b1), .clk(Clk), .Q(R0_q));  // open: clr
  Register #(.width(32)) R1 (.D(BusW), .en(and_1_out), .clk(Clk), .Q(R1_q));  // open: clr
  Register #(.width(32)) R2 (.D(BusW), .en(and_2_out), .clk(Clk), .Q(R2_q));  // open: clr
  Register #(.width(32)) R3 (.D(BusW), .en(and_3_out), .clk(Clk), .Q(R3_q));  // open: clr
  Register #(.width(32)) R4 (.D(BusW), .en(and_4_out), .clk(Clk), .Q(R4_q));  // open: clr
  Register #(.width(32)) R5 (.D(BusW), .en(and_5_out), .clk(Clk), .Q(R5_q));  // open: clr
  Register #(.width(32)) R6 (.D(BusW), .en(and_6_out), .clk(Clk), .Q(R6_q));  // open: clr
  Register #(.width(32)) R7 (.D(BusW), .en(and_7_out), .clk(Clk), .Q(R7_q));  // open: clr
  Register #(.width(32)) R8 (.D(BusW), .en(and_8_out), .clk(Clk), .Q(R8_q));  // open: clr
  Register #(.width(32)) R9 (.D(BusW), .en(and_9_out), .clk(Clk), .Q(R9_q));  // open: clr
  Register #(.width(32)) R10 (.D(BusW), .en(and_10_out), .clk(Clk), .Q(R10_q));  // open: clr
  Register #(.width(32)) R11 (.D(BusW), .en(and_11_out), .clk(Clk), .Q(R11_q));  // open: clr
  Register #(.width(32)) R12 (.D(BusW), .en(and_12_out), .clk(Clk), .Q(R12_q));  // open: clr
  Register #(.width(32)) R13 (.D(BusW), .en(and_13_out), .clk(Clk), .Q(R13_q));  // open: clr
  Register #(.width(32)) R14 (.D(BusW), .en(and_14_out), .clk(Clk), .Q(R14_q));  // open: clr
  Register #(.width(32)) R15 (.D(BusW), .en(and_15_out), .clk(Clk), .Q(R15_q));  // open: clr
  Register #(.width(32)) R16 (.D(BusW), .en(and_16_out), .clk(Clk));  // open: Q, clr
  Register #(.width(32)) R17 (.D(BusW), .en(and_17_out), .clk(Clk));  // open: Q, clr
  Register #(.width(32)) R18 (.D(BusW), .en(and_18_out), .clk(Clk), .Q(R18_q));  // open: clr
  Register #(.width(32)) R19 (.D(BusW), .en(and_19_out), .clk(Clk), .Q(R19_q));  // open: clr
  Register #(.width(32)) R20 (.D(BusW), .en(and_20_out), .clk(Clk), .Q(R20_q));  // open: clr
  Register #(.width(32)) R21 (.D(BusW), .en(and_21_out), .clk(Clk), .Q(R21_q));  // open: clr
  Register #(.width(32)) R22 (.D(BusW), .en(and_22_out), .clk(Clk), .Q(R22_q));  // open: clr
  Register #(.width(32)) R23 (.D(BusW), .en(and_23_out), .clk(Clk), .Q(R23_q));  // open: clr
  Register #(.width(32)) R24 (.D(BusW), .en(and_24_out), .clk(Clk), .Q(R24_q));  // open: clr
  Register #(.width(32)) R25 (.D(BusW), .en(and_25_out), .clk(Clk), .Q(R25_q));  // open: clr
  Register #(.width(32)) R26 (.D(BusW), .en(and_26_out), .clk(Clk), .Q(R26_q));  // open: clr
  Register #(.width(32)) R27 (.D(BusW), .en(and_27_out), .clk(Clk), .Q(R27_q));  // open: clr
  Register #(.width(32)) R28 (.D(BusW), .en(and_28_out), .clk(Clk), .Q(R28_q));  // open: clr
  Register #(.width(32)) R29 (.D(BusW), .en(and_29_out), .clk(Clk), .Q(R29_q));  // open: clr
  Register #(.width(32)) R30 (.D(BusW), .en(and_30_out), .clk(Clk), .Q(R30_q));  // open: clr
  Register #(.width(32)) R31 (.D(BusW), .en(and_31_out), .clk(Clk), .Q(R31_q));  // open: clr
  Decoder #(.enable("false"), .select(5)) decoder_2 (
    .out0(decoder_2_out0), .out1(decoder_2_out1), .out2(decoder_2_out2), .out3(decoder_2_out3),
    .out4(decoder_2_out4), .out5(decoder_2_out5), .out6(decoder_2_out6), .out7(decoder_2_out7),
    .out8(decoder_2_out8), .out9(decoder_2_out9), .out10(decoder_2_out10), .out11(decoder_2_out11),
    .out12(decoder_2_out12), .out13(decoder_2_out13), .out14(decoder_2_out14), .out15(decoder_2_out15),
    .out16(decoder_2_out16), .out17(decoder_2_out17), .out18(decoder_2_out18), .out19(decoder_2_out19),
    .out20(decoder_2_out20), .out21(decoder_2_out21), .out22(decoder_2_out22), .out23(decoder_2_out23),
    .out24(decoder_2_out24), .out25(decoder_2_out25), .out26(decoder_2_out26), .out27(decoder_2_out27),
    .out28(decoder_2_out28), .out29(decoder_2_out29), .out30(decoder_2_out30), .out31(decoder_2_out31),
    .sel(RA));
  assign BusA = decoder_2_out0 ? R0_q : 32'bz;  // Controlled_Buffer controlled_buffer_1
  assign BusA = decoder_2_out1 ? R1_q : 32'bz;  // Controlled_Buffer controlled_buffer_2
  assign BusA = decoder_2_out2 ? R2_q : 32'bz;  // Controlled_Buffer controlled_buffer_3
  assign BusA = decoder_2_out3 ? R3_q : 32'bz;  // Controlled_Buffer controlled_buffer_4
  assign BusA = decoder_2_out4 ? R4_q : 32'bz;  // Controlled_Buffer controlled_buffer_5
  assign BusA = decoder_2_out5 ? R5_q : 32'bz;  // Controlled_Buffer controlled_buffer_6
  assign BusA = decoder_2_out6 ? R6_q : 32'bz;  // Controlled_Buffer controlled_buffer_7
  assign BusA = decoder_2_out7 ? R7_q : 32'bz;  // Controlled_Buffer controlled_buffer_8
  assign BusA = decoder_2_out8 ? R8_q : 32'bz;  // Controlled_Buffer controlled_buffer_9
  assign BusA = decoder_2_out9 ? R9_q : 32'bz;  // Controlled_Buffer controlled_buffer_10
  assign BusA = decoder_2_out10 ? R10_q : 32'bz;  // Controlled_Buffer controlled_buffer_11
  assign BusA = decoder_2_out11 ? R11_q : 32'bz;  // Controlled_Buffer controlled_buffer_12
  assign BusA = decoder_2_out12 ? R12_q : 32'bz;  // Controlled_Buffer controlled_buffer_13
  assign BusA = decoder_2_out13 ? R13_q : 32'bz;  // Controlled_Buffer controlled_buffer_14
  assign BusA = decoder_2_out14 ? R14_q : 32'bz;  // Controlled_Buffer controlled_buffer_15
  assign BusA = decoder_2_out15 ? R15_q : 32'bz;  // Controlled_Buffer controlled_buffer_16
  assign BusA = decoder_2_out16 ? undriven : 32'bz;  // Controlled_Buffer controlled_buffer_17
  assign BusA = decoder_2_out17 ? undriven_2 : 32'bz;  // Controlled_Buffer controlled_buffer_18
  assign BusA = decoder_2_out18 ? R18_q : 32'bz;  // Controlled_Buffer controlled_buffer_19
  assign BusA = decoder_2_out19 ? R19_q : 32'bz;  // Controlled_Buffer controlled_buffer_20
  assign BusA = decoder_2_out20 ? R20_q : 32'bz;  // Controlled_Buffer controlled_buffer_21
  assign BusA = decoder_2_out21 ? R21_q : 32'bz;  // Controlled_Buffer controlled_buffer_22
  assign BusA = decoder_2_out22 ? R22_q : 32'bz;  // Controlled_Buffer controlled_buffer_23
  assign BusA = decoder_2_out23 ? R23_q : 32'bz;  // Controlled_Buffer controlled_buffer_24
  assign BusA = decoder_2_out24 ? R24_q : 32'bz;  // Controlled_Buffer controlled_buffer_25
  assign BusA = decoder_2_out25 ? R25_q : 32'bz;  // Controlled_Buffer controlled_buffer_26
  assign BusA = decoder_2_out26 ? R26_q : 32'bz;  // Controlled_Buffer controlled_buffer_27
  assign BusA = decoder_2_out27 ? R27_q : 32'bz;  // Controlled_Buffer controlled_buffer_28
  assign BusA = decoder_2_out28 ? R28_q : 32'bz;  // Controlled_Buffer controlled_buffer_29
  assign BusA = decoder_2_out29 ? R29_q : 32'bz;  // Controlled_Buffer controlled_buffer_30
  assign BusA = decoder_2_out30 ? R30_q : 32'bz;  // Controlled_Buffer controlled_buffer_31
  assign BusA = decoder_2_out31 ? R31_q : 32'bz;  // Controlled_Buffer controlled_buffer_32
  Decoder #(.enable("false"), .select(5)) decoder_3 (
    .out0(decoder_3_out0), .out1(decoder_3_out1), .out2(decoder_3_out2), .out3(decoder_3_out3),
    .out4(decoder_3_out4), .out5(decoder_3_out5), .out6(decoder_3_out6), .out7(decoder_3_out7),
    .out8(decoder_3_out8), .out9(decoder_3_out9), .out10(decoder_3_out10), .out11(decoder_3_out11),
    .out12(decoder_3_out12), .out13(decoder_3_out13), .out14(decoder_3_out14), .out15(decoder_3_out15),
    .out16(decoder_3_out16), .out17(decoder_3_out17), .out18(decoder_3_out18), .out19(decoder_3_out19),
    .out20(decoder_3_out20), .out21(decoder_3_out21), .out22(decoder_3_out22), .out23(decoder_3_out23),
    .out24(decoder_3_out24), .out25(decoder_3_out25), .out26(decoder_3_out26), .out27(decoder_3_out27),
    .out28(decoder_3_out28), .out29(decoder_3_out29), .out30(decoder_3_out30), .out31(decoder_3_out31),
    .sel(RB));
  assign BusB = decoder_3_out0 ? R0_q : 32'bz;  // Controlled_Buffer controlled_buffer_33
  assign BusB = decoder_3_out1 ? R1_q : 32'bz;  // Controlled_Buffer controlled_buffer_34
  assign BusB = decoder_3_out2 ? R2_q : 32'bz;  // Controlled_Buffer controlled_buffer_35
  assign BusB = decoder_3_out3 ? R3_q : 32'bz;  // Controlled_Buffer controlled_buffer_36
  assign BusB = decoder_3_out4 ? R4_q : 32'bz;  // Controlled_Buffer controlled_buffer_37
  assign BusB = decoder_3_out5 ? R5_q : 32'bz;  // Controlled_Buffer controlled_buffer_38
  assign BusB = decoder_3_out6 ? R6_q : 32'bz;  // Controlled_Buffer controlled_buffer_39
  assign BusB = decoder_3_out7 ? R7_q : 32'bz;  // Controlled_Buffer controlled_buffer_40
  assign BusB = decoder_3_out8 ? R8_q : 32'bz;  // Controlled_Buffer controlled_buffer_41
  assign BusB = decoder_3_out9 ? R9_q : 32'bz;  // Controlled_Buffer controlled_buffer_42
  assign BusB = decoder_3_out10 ? R10_q : 32'bz;  // Controlled_Buffer controlled_buffer_43
  assign BusB = decoder_3_out11 ? R11_q : 32'bz;  // Controlled_Buffer controlled_buffer_44
  assign BusB = decoder_3_out12 ? R12_q : 32'bz;  // Controlled_Buffer controlled_buffer_45
  assign BusB = decoder_3_out13 ? R13_q : 32'bz;  // Controlled_Buffer controlled_buffer_46
  assign BusB = decoder_3_out14 ? R14_q : 32'bz;  // Controlled_Buffer controlled_buffer_47
  assign BusB = decoder_3_out15 ? R15_q : 32'bz;  // Controlled_Buffer controlled_buffer_48
  assign BusB = decoder_3_out16 ? undriven : 32'bz;  // Controlled_Buffer controlled_buffer_49
  assign BusB = decoder_3_out17 ? undriven_2 : 32'bz;  // Controlled_Buffer controlled_buffer_50
  assign BusB = decoder_3_out18 ? R18_q : 32'bz;  // Controlled_Buffer controlled_buffer_51
  assign BusB = decoder_3_out19 ? R19_q : 32'bz;  // Controlled_Buffer controlled_buffer_52
  assign BusB = decoder_3_out20 ? R20_q : 32'bz;  // Controlled_Buffer controlled_buffer_53
  assign BusB = decoder_3_out21 ? R21_q : 32'bz;  // Controlled_Buffer controlled_buffer_54
  assign BusB = decoder_3_out22 ? R22_q : 32'bz;  // Controlled_Buffer controlled_buffer_55
  assign BusB = decoder_3_out23 ? R23_q : 32'bz;  // Controlled_Buffer controlled_buffer_56
  assign BusB = decoder_3_out24 ? R24_q : 32'bz;  // Controlled_Buffer controlled_buffer_57
  assign BusB = decoder_3_out25 ? R25_q : 32'bz;  // Controlled_Buffer controlled_buffer_58
  assign BusB = decoder_3_out26 ? R26_q : 32'bz;  // Controlled_Buffer controlled_buffer_59
  assign BusB = decoder_3_out27 ? R27_q : 32'bz;  // Controlled_Buffer controlled_buffer_60
  assign BusB = decoder_3_out28 ? R28_q : 32'bz;  // Controlled_Buffer controlled_buffer_61
  assign BusB = decoder_3_out29 ? R29_q : 32'bz;  // Controlled_Buffer controlled_buffer_62
  assign BusB = decoder_3_out30 ? R30_q : 32'bz;  // Controlled_Buffer controlled_buffer_63
  assign BusB = decoder_3_out31 ? R31_q : 32'bz;  // Controlled_Buffer controlled_buffer_64

  // Other names for the same wires on the sheet: RegWrite = EnableWrite
endmodule

module Shifter (
  input  [4:0] ShiftVal,
  input  [31:0] Data,
  input  [1:0] ShiftOp,
  output [31:0] Data_Out
);

  wire EnableSLL;
  wire [4:0] bit_extender_1_out, xor_1_out;
  wire [32:0] multiplexer_5_out;
  wire [34:0] multiplexer_4_out;
  wire [38:0] multiplexer_3_out;
  wire [46:0] multiplexer_1_out, multiplexer_2_out;
  wire [46:31] multiplexer_1_out_2;
  wire [62:0] bit_extender_2_out, bit_extender_3_out;

  assign bit_extender_1_out = {{4{EnableSLL}}, EnableSLL};  // Bit_Extender bit_extender_1
  assign xor_1_out = ShiftVal ^ bit_extender_1_out;  // XOR_Gate xor_1, 5 bits wide
  nor nor_1 (EnableSLL, ShiftOp[0], ShiftOp[1]);
  assign bit_extender_2_out = {{31{1'b0}}, Data};  // Bit_Extender bit_extender_2
  assign bit_extender_3_out = {{31{Data[31]}}, Data};  // Bit_Extender bit_extender_3
  Multiplexer #(.select(2), .width(63)) multiplexer_1 (
    .in0({Data, {31{1'b0}}}), .in1(bit_extender_2_out), .in2(bit_extender_3_out), .in3({Data[30:0], Data}),
    .out({multiplexer_1_out_2, multiplexer_1_out}), .sel(ShiftOp));
  Multiplexer #(.width(47)) multiplexer_2 (
    .in0(multiplexer_1_out), .in1({multiplexer_1_out_2, multiplexer_1_out[46:16]}), .out(multiplexer_2_out),
    .sel(xor_1_out[4]));
  Multiplexer #(.width(39)) multiplexer_3 (
    .in0(multiplexer_2_out[38:0]), .in1(multiplexer_2_out[46:8]), .out(multiplexer_3_out), .sel(xor_1_out[3]));
  Multiplexer #(.width(35)) multiplexer_4 (
    .in0(multiplexer_3_out[34:0]), .in1(multiplexer_3_out[38:4]), .out(multiplexer_4_out), .sel(xor_1_out[2]));
  Multiplexer #(.width(33)) multiplexer_5 (
    .in0(multiplexer_4_out[32:0]), .in1(multiplexer_4_out[34:2]), .out(multiplexer_5_out), .sel(xor_1_out[1]));
  Multiplexer #(.width(32)) multiplexer_6 (
    .in0(multiplexer_5_out[31:0]), .in1(multiplexer_5_out[32:1]), .out(Data_Out), .sel(xor_1_out[0]));

  // Notes on the sheet:
  //   SLL = 00
  //   SRL = 01
  //   SRA = 10
  //   ROR = 11
endmodule

module Sign (
  input  Data,
  input  Overflow,
  output [31:0] Data_Out
);

  wire xnor_1_out;

  xnor xnor_1 (xnor_1_out, Data, Overflow);
  assign Data_Out = {{31{1'b0}}, xnor_1_out};  // Bit_Extender bit_extender_1
endmodule
