// Logisim project CPU_MIPS_divisionPIPELINED_FIXEDdataHAZARD.circ as structural Verilog: 10 circuits, main circuit ALU_MIPS
module main (
);

  wire alu_mips_1_zero, ALUsrc, clock_1_out, ExtOp, MemRead, MemtoReg, MemWrite, nextpc_1_pcsrc, RegDst,
       RegWrite;
  wire [0:0] register_5_q;
  wire [2:0] J_Beq_Bne, main_control_1_j_beq_bne;
  wire [4:0] hazarddetector_1_p5, hazarddetector_1_p6, multiplexer_2_out, register_10_q;
  wire [5:0] func, OP;
  wire [6:0] aluctrl_1_aluop, ALUop;
  wire [8:0] main_control_1_alusrc;
  wire [8:5] register_2_q;
  wire [15:0] register_8_q;
  wire [21:0] multiplexer_1_out, nextpc_1_jumped_address, plus_one_1_out_2, register_1_q, register_3_q,
       register_7_q;
  wire [25:6] register_4_q;
  wire [25:16] register_8_q_2;
  wire [29:0] bit_extender_1_out;
  wire [29:22] nextpc_1_jumped_address_2;
  wire [31:0] alu_mips_1_alu_result, bit_extender_2_out, bit_extender_3_out, multiplexer_3_out,
       multiplexer_4_out, multiplexer_5_out, multiplexer_6_out, multiplexer_7_out, ram_1_dout, register_9_q,
       register_11_q, register_12_q, register_13_q, register_15_q, registers_file_1_busa,
       registers_file_1_busb, rom_1_data;

  Multiplexer #(.width(22)) multiplexer_1 (
    .in0(plus_one_1_out_2), .in1(nextpc_1_jumped_address), .out(multiplexer_1_out));  // open: sel
  Register #(.width(22)) register_1 (.D(multiplexer_1_out), .Q(register_1_q), .clk(clock_1_out));  // open: en, clr
  Clock clock_1 (.out(clock_1_out));
  Main_Control main_control_1 (
    .OP(OP), .ALUsrc(main_control_1_alusrc[0]), .ExtOp(main_control_1_alusrc[1]), .RegDst(RegDst),
    .J_Beq_Bne(main_control_1_j_beq_bne), .RegWrite(main_control_1_alusrc[5]),
    .MemRead(main_control_1_alusrc[6]), .MemWrite(main_control_1_alusrc[7]), .MemReg(main_control_1_alusrc[8]));
  ALUctrl aluctrl_1 (.func(func), .OP(OP), .ALUop(aluctrl_1_aluop));
  plus_one plus_one_1 (.out_2(plus_one_1_out_2), .in_1(register_1_q));
  ROM #(.addrWidth(24), .dataWidth(32)) rom_1 (.addr({register_1_q, 2'b00}), .data(rom_1_data));
  Register #(.width(16)) register_2 (
    .D({aluctrl_1_aluop, main_control_1_alusrc[8:5], main_control_1_j_beq_bne, main_control_1_alusrc[1:0]}),
    .Q({ALUop, register_2_q, J_Beq_Bne, ExtOp, ALUsrc}), .clk(clock_1_out));  // open: en, clr
  Register #(.width(22)) register_3 (.D(plus_one_1_out_2), .Q(register_3_q));  // open: en, clk, clr
  Register #(.width(32)) register_4 (.D(rom_1_data), .Q({OP, register_4_q, func}), .clk(clock_1_out));  // open: en, clr
  Register #(.width(4)) register_5 (
    .D(register_2_q), .Q({MemtoReg, MemWrite, MemRead, register_5_q[0]}), .clk(clock_1_out));  // open: en, clr
  Multiplexer #(.width(5)) multiplexer_2 (
    .in0(register_4_q[20:16]), .in1(register_4_q[15:11]), .out(multiplexer_2_out), .sel(RegDst));
  Registers_file registers_file_1 (
    .BusA(registers_file_1_busa), .BusB(registers_file_1_busb), .RegWrite(RegWrite), .Clock(clock_1_out),
    .BusW(register_15_q), .RB_address(register_4_q[20:16]), .RA_address(register_4_q[25:21]),
    .RW_address(hazarddetector_1_p6));
  Register #(.width(1)) register_6 (.D(register_5_q[0]), .Q(RegWrite), .clk(clock_1_out));  // open: en, clr
  Register #(.width(22)) register_7 (.D(register_3_q), .Q(register_7_q), .clk(clock_1_out));  // open: en, clr
  Register #(.width(26)) register_8 (
    .D({register_4_q, func}), .Q({register_8_q_2, register_8_q}), .clk(clock_1_out));  // open: en, clr
  Multiplexer #(.select(2), .width(32)) multiplexer_3 (
    .in0(registers_file_1_busa), .in1(alu_mips_1_alu_result), .in2(multiplexer_7_out), .in3(register_15_q),
    .out(multiplexer_3_out), .sel(2'b00));
  Multiplexer #(.select(2), .width(32)) multiplexer_4 (
    .in0(registers_file_1_busb), .in1(alu_mips_1_alu_result), .in2(multiplexer_7_out), .in3(register_15_q),
    .out(multiplexer_4_out), .sel(2'b00));
  Register #(.width(32)) register_9 (.D(multiplexer_4_out), .Q(register_9_q), .clk(clock_1_out));  // open: en, clr
  Register #(.width(5)) register_10 (.D(multiplexer_2_out), .Q(register_10_q), .clk(clock_1_out));  // open: en, clr
  assign bit_extender_1_out = {{8{register_7_q[21]}}, register_7_q};  // Bit_Extender bit_extender_1
  assign bit_extender_2_out = {{16{1'b0}}, register_8_q};  // Bit_Extender bit_extender_2
  assign bit_extender_3_out = {{16{register_8_q[15]}}, register_8_q};  // Bit_Extender bit_extender_3
  Register #(.width(32)) register_11 (.D(multiplexer_3_out), .Q(register_11_q), .clk(clock_1_out));  // open: en, clr
  Multiplexer #(.width(32)) multiplexer_5 (
    .in0(register_9_q), .in1(multiplexer_6_out), .out(multiplexer_5_out), .sel(ALUsrc));
  Multiplexer #(.width(32)) multiplexer_6 (
    .in0(bit_extender_2_out), .in1(bit_extender_3_out), .out(multiplexer_6_out), .sel(ExtOp));
  ALU_MIPS alu_mips_1 (
    .zero(alu_mips_1_zero), .ALU_result(alu_mips_1_alu_result), .Data_B(multiplexer_5_out),
    .Data_A(register_11_q), .ALUctrl(ALUop));  // open: overflow
  // HazardDetector hazarddetector_1: pin names not known; wires that end beside it: register_4_q[20:16], register_4_q[25:21], 2'b00, register_10_q, hazarddetector_1_p5, hazarddetector_1_p6, RegWrite, register_5_q[0], register_2_q[5]
  NextPc nextpc_1 (
    .PcSrc(nextpc_1_pcsrc), .Jumped_Address({nextpc_1_jumped_address_2, nextpc_1_jumped_address}),
    .PC_inc(bit_extender_1_out), .Imm26({register_8_q_2, register_8_q}), .J(J_Beq_Bne[0]),
    .Zero(alu_mips_1_zero), .Bne(J_Beq_Bne[2]), .Beq(J_Beq_Bne[1]));
  Register #(.width(32)) register_12 (
    .D(alu_mips_1_alu_result), .Q(register_12_q), .clk(clock_1_out));  // open: en, clr
  Register #(.width(32)) register_13 (.D(register_9_q), .Q(register_13_q), .clk(clock_1_out));  // open: en, clr
  Register #(.width(5)) register_14 (.D(register_10_q), .Q(hazarddetector_1_p5), .clk(clock_1_out));  // open: en, clr
  RAM #(.addrWidth(24), .dataWidth(32)) ram_1 (
    .addr(register_12_q[23:0]), .we(MemWrite), .oe(MemRead), .clk(clock_1_out), .din(register_13_q),
    .dout(ram_1_dout));
  Multiplexer #(.width(32)) multiplexer_7 (
    .in0(register_12_q), .in1(ram_1_dout), .out(multiplexer_7_out), .sel(MemtoReg));
  Register #(.width(32)) register_15 (.D(multiplexer_7_out), .Q(register_15_q), .clk(clock_1_out));  // open: en, clr
  Register #(.width(5)) register_16 (
    .D(hazarddetector_1_p5), .Q(hazarddetector_1_p6), .clk(clock_1_out));  // open: en, clr

  // Notes on the sheet:
  //   Comments:
  //   Solutions:
  //   1- Adding no-op as said.
  //   2- add two no-op after each and every jump/branch operation.
  //   contents of rom_1 (hex, n*v repeats v):
  //   8100001 51*0 a0080000 4194251*0 1004024 0 0 0 1204824 0 0 0 1405024 0 0 0 21290079 0 0 0 200a000c 0
  //   0 0 1605824 0 0 0 12a4822 0 0 0 21080001 0 0 0 6024 0 0 0 6024 0 0 0 6024 0 0 0 6024 0 0 0 114bfff8
  //   0 0 0 6024 0 0 0 6024 0 0 0 6024 0 0 0 6024 0 0 0 6024 0 0 0 112b000a 0 0 0 6024 0 0 0 6024 0 0 0
  //   6024 0 0 0 6024 0 0 0 216b0001 0 0 0 6024 0 0 0 6024 0 0 0 6024 0 0 0 6024 0 0 0 8100008 0 0 0
  //   ac080000 0 0 0 ac090004 0 0 0 6024
  //   1- In the first sub operation register 10 needed value will be late. therefor a usless loop will happen and in turn the counter will be added by an uneeded 1. in brief, we will do a usless sub and this will be like if we done sub 11 times instead of the correct 10 times.
  //   Answers are 10 and 1. they can be found in the RAM on addresses 0x0 and 0x20
  //   2- After every jump or branch operation, the following two instructions will pass. this will add to the remainder an uneeded 1 which in the end will make the remainder true result added by one. also, this jump/branch error causes an infinte loop. by the time we want to branch to the end of the program, we pass two operations after this branch which we should not. this passes a jump operation to a new loop itteration, causing an infinte loop.
endmodule

module ALU_MIPS (
  input  [6:0] ALUctrl,
  input  [31:0] Data_A,
  input  [31:0] Data_B,
  output [31:0] ALU_result,
  output overflow,
  output zero
);

  wire xor_3_out;
  wire [31:0] adder_1_out, and_1_out, bit_extender_1_out, bit_extender_2_out, multiplexer_1_out, not_1_out,
       or_1_out, shifter_custom_1_out_4, xor_1_out, xor_2_out;

  assign bit_extender_1_out = {{31{ALUctrl[2]}}, ALUctrl[2]};  // Bit_Extender bit_extender_1
  assign xor_1_out = Data_B ^ bit_extender_1_out;  // XOR_Gate xor_1, 32 bits wide
  assign and_1_out = Data_A & Data_B;  // AND_Gate and_1, 32 bits wide
  assign or_1_out = Data_A | Data_B;  // OR_Gate or_1, 32 bits wide
  assign xor_2_out = Data_A ^ Data_B;  // XOR_Gate xor_2, 32 bits wide
  assign not_1_out = ~or_1_out;  // NOT_Gate not_1, 32 bits wide
  Shifter_custom shifter_custom_1 (.Data(Data_B), .OP(ALUctrl[1:0]), .SA(Data_A[4:0]), .out_4(shifter_custom_1_out_4));
  Adder #(.width(32)) adder_1 (.a(Data_A), .b(xor_1_out), .out(adder_1_out), .cin(ALUctrl[2]), .cout(overflow));
  Multiplexer #(.select(2), .width(32)) multiplexer_1 (
    .in0(and_1_out), .in1(or_1_out), .in2(not_1_out), .in3(xor_2_out), .out(multiplexer_1_out),
    .sel(ALUctrl[4:3]));
  assign bit_extender_2_out = {{31{xor_3_out}}, xor_3_out};  // Bit_Extender bit_extender_2
  xor xor_3 (xor_3_out, adder_1_out[31], overflow);
  Multiplexer #(.select(2), .width(32)) multiplexer_2 (
    .in0(shifter_custom_1_out_4), .in1(bit_extender_2_out), .in2(adder_1_out), .in3(multiplexer_1_out),
    .out(ALU_result), .sel(ALUctrl[6:5]));
  nor nor_1 (zero, ALU_result[0], ALU_result[1], ALU_result[2], ALU_result[3], ALU_result[4], ALU_result[5], ALU_result[6], ALU_result[7], ALU_result[8], ALU_result[9], ALU_result[10], ALU_result[11], ALU_result[12], ALU_result[13], ALU_result[14], ALU_result[15], ALU_result[16], ALU_result[17], ALU_result[18], ALU_result[19], ALU_result[20], ALU_result[21], ALU_result[22], ALU_result[23], ALU_result[24], ALU_result[25], ALU_result[26], ALU_result[27], ALU_result[28], ALU_result[29], ALU_result[30], ALU_result[31]);
endmodule

module Shifter_custom (
  input  [31:0] Data,
  input  [1:0] OP,
  input  [4:0] SA,
  output [31:0] out_4
);

  wire and_1_out, not_1_out;
  wire [1:0] multiplexer_3_out, multiplexer_3_out_3;
  wire [4:0] bit_extender_1_out, xor_1_out;
  wire [30:0] multiplexer_3_out_2;
  wire [32:0] multiplexer_4_out;
  wire [38:0] multiplexer_2_out;
  wire [46:0] multiplexer_1_out;
  wire [62:0] extender_custom_1_out_3;

  not not_1 (not_1_out, OP[1]);
  and and_1 (and_1_out, OP[0], not_1_out);
  assign bit_extender_1_out = {{4{and_1_out}}, and_1_out};  // Bit_Extender bit_extender_1
  assign xor_1_out = SA ^ bit_extender_1_out;  // XOR_Gate xor_1, 5 bits wide
  Extender_custom extender_custom_1 (.in_1(Data), .in_2(OP), .out_3(extender_custom_1_out_3));
  Multiplexer #(.width(47)) multiplexer_1 (
    .in0(extender_custom_1_out_3[46:0]), .in1(extender_custom_1_out_3[62:16]), .out(multiplexer_1_out),
    .sel(xor_1_out[4]));
  Multiplexer #(.width(39)) multiplexer_2 (
    .in0(multiplexer_1_out[38:0]), .in1(multiplexer_1_out[46:8]), .out(multiplexer_2_out), .sel(xor_1_out[3]));
  Multiplexer #(.width(35)) multiplexer_3 (
    .in0(multiplexer_2_out[34:0]), .in1(multiplexer_2_out[38:4]),
    .out({multiplexer_3_out_3, multiplexer_3_out_2, multiplexer_3_out}), .sel(xor_1_out[2]));
  Multiplexer #(.width(33)) multiplexer_4 (
    .in0({multiplexer_3_out_2, multiplexer_3_out}), .in1({multiplexer_3_out_3, multiplexer_3_out_2}),
    .out(multiplexer_4_out), .sel(xor_1_out[1]));
  Multiplexer #(.width(32)) multiplexer_5 (
    .in0(multiplexer_4_out[31:0]), .in1(multiplexer_4_out[32:1]), .out(out_4), .sel(xor_1_out[0]));
endmodule

module Extender_custom (
  input  [31:0] in_1,
  input  [1:0] in_2,
  output [62:0] out_3
);

  wire [62:0] bit_extender_1_out;

  assign bit_extender_1_out = {{31{in_1[31]}}, in_1};  // Bit_Extender bit_extender_1
  Multiplexer #(.select(2), .width(63)) multiplexer_1 (
    .in0({in_1, {31{1'b0}}}), .in1({{31{1'b0}}, in_1}), .in2(bit_extender_1_out), .in3({in_1[30:0], in_1}),
    .out(out_3), .sel(in_2));
endmodule

module Registers_file (
  input  Clock,
  input  RegWrite,
  input  [4:0] RA_address,
  input  [4:0] RB_address,
  input  [4:0] RW_address,
  input  [31:0] BusW,
  output [31:0] BusA,
  output [31:0] BusB
);

  wire and_1_out, and_2_out, and_3_out, and_4_out, and_5_out, and_6_out, and_7_out, and_8_out, and_9_out,
       and_10_out, and_11_out, and_12_out, and_13_out, and_14_out, and_15_out, and_16_out, and_17_out,
       and_18_out, and_19_out, and_20_out, and_21_out, and_22_out, and_23_out, and_24_out, and_25_out,
       and_26_out, and_27_out, and_28_out, and_29_out, and_30_out, and_31_out, and_32_out, decoder_1_out0,
       decoder_1_out1, decoder_1_out2, decoder_1_out3, decoder_1_out4, decoder_1_out5, decoder_1_out6,
       decoder_1_out7, decoder_1_out8, decoder_1_out9, decoder_1_out10, decoder_1_out11, decoder_1_out12,
       decoder_1_out13, decoder_1_out14, decoder_1_out15, decoder_1_out16, decoder_1_out17, decoder_1_out18,
       decoder_1_out19, decoder_1_out20, decoder_1_out21, decoder_1_out22, decoder_1_out23, decoder_1_out24,
       decoder_1_out25, decoder_1_out26, decoder_1_out27, decoder_1_out28, decoder_1_out29, decoder_1_out30,
       decoder_1_out31;
  wire [31:0] register_1_q, register_2_q, register_3_q, register_4_q, register_5_q, register_6_q,
       register_7_q, register_8_q, register_9_q, register_10_q, register_11_q, register_12_q, register_13_q,
       register_14_q, register_15_q, register_16_q, register_17_q, register_18_q, register_19_q,
       register_20_q, register_21_q, register_22_q, register_23_q, register_24_q, register_25_q,
       register_26_q, register_27_q, register_28_q, register_29_q, register_30_q, register_31_q,
       register_32_q;

  Decoder #(.select(5)) decoder_1 (
    .out0(decoder_1_out0), .out1(decoder_1_out1), .out2(decoder_1_out2), .out3(decoder_1_out3),
    .out4(decoder_1_out4), .out5(decoder_1_out5), .out6(decoder_1_out6), .out7(decoder_1_out7),
    .out8(decoder_1_out8), .out9(decoder_1_out9), .out10(decoder_1_out10), .out11(decoder_1_out11),
    .out12(decoder_1_out12), .out13(decoder_1_out13), .out14(decoder_1_out14), .out15(decoder_1_out15),
    .out16(decoder_1_out16), .out17(decoder_1_out17), .out18(decoder_1_out18), .out19(decoder_1_out19),
    .out20(decoder_1_out20), .out21(decoder_1_out21), .out22(decoder_1_out22), .out23(decoder_1_out23),
    .out24(decoder_1_out24), .out25(decoder_1_out25), .out26(decoder_1_out26), .out27(decoder_1_out27),
    .out28(decoder_1_out28), .out29(decoder_1_out29), .out30(decoder_1_out30), .out31(decoder_1_out31),
    .sel(RW_address), .en(1'b1));
  and and_1 (and_1_out, RegWrite, decoder_1_out0);
  and and_2 (and_2_out, RegWrite, decoder_1_out2);
  and and_3 (and_3_out, RegWrite, decoder_1_out4);
  and and_4 (and_4_out, RegWrite, decoder_1_out6);
  and and_5 (and_5_out, RegWrite, decoder_1_out8);
  and and_6 (and_6_out, RegWrite, decoder_1_out10);
  and and_7 (and_7_out, RegWrite, decoder_1_out12);
  and and_8 (and_8_out, RegWrite, decoder_1_out14);
  and and_9 (and_9_out, RegWrite, decoder_1_out16);
  and and_10 (and_10_out, RegWrite, decoder_1_out18);
  and and_11 (and_11_out, RegWrite, decoder_1_out20);
  and and_12 (and_12_out, RegWrite, decoder_1_out22);
  and and_13 (and_13_out, RegWrite, decoder_1_out24);
  and and_14 (and_14_out, RegWrite, decoder_1_out26);
  and and_15 (and_15_out, RegWrite, decoder_1_out28);
  and and_16 (and_16_out, RegWrite, decoder_1_out30);
  Register #(.width(32)) register_1 (.D({32{1'b0}}), .en(and_1_out), .Q(register_1_q), .clk(Clock));  // open: clr
  and and_17 (and_17_out, RegWrite, decoder_1_out1);
  Register #(.width(32)) register_2 (.D(BusW), .en(and_2_out), .Q(register_2_q), .clk(Clock));  // open: clr
  and and_18 (and_18_out, RegWrite, decoder_1_out3);
  Register #(.width(32)) register_3 (.D(BusW), .en(and_3_out), .Q(register_3_q), .clk(Clock));  // open: clr
  and and_19 (and_19_out, RegWrite, decoder_1_out5);
  Register #(.width(32)) register_4 (.D(BusW), .en(and_4_out), .Q(register_4_q), .clk(Clock));  // open: clr
  and and_20 (and_20_out, RegWrite, decoder_1_out7);
  Register #(.width(32)) register_5 (.D(BusW), .en(and_5_out), .Q(register_5_q), .clk(Clock));  // open: clr
  and and_21 (and_21_out, RegWrite, decoder_1_out9);
  Register #(.width(32)) register_6 (.D(BusW), .en(and_6_out), .Q(register_6_q), .clk(Clock));  // open: clr
  and and_22 (and_22_out, RegWrite, decoder_1_out11);
  Register #(.width(32)) register_7 (.D(BusW), .en(and_7_out), .Q(register_7_q), .clk(Clock));  // open: clr
  and and_23 (and_23_out, RegWrite, decoder_1_out13);
  Register #(.width(32)) register_8 (.D(BusW), .en(and_8_out), .Q(register_8_q), .clk(Clock));  // open: clr
  and and_24 (and_24_out, RegWrite, decoder_1_out15);
  Register #(.width(32)) register_9 (.D(BusW), .en(and_9_out), .Q(register_9_q), .clk(Clock));  // open: clr
  and and_25 (and_25_out, RegWrite, decoder_1_out17);
  Register #(.width(32)) register_10 (.D(BusW), .en(and_10_out), .Q(register_10_q), .clk(Clock));  // open: clr
  and and_26 (and_26_out, RegWrite, decoder_1_out19);
  Register #(.width(32)) register_11 (.D(BusW), .en(and_11_out), .Q(register_11_q), .clk(Clock));  // open: clr
  and and_27 (and_27_out, RegWrite, decoder_1_out21);
  Register #(.width(32)) register_12 (.D(BusW), .en(and_12_out), .Q(register_12_q), .clk(Clock));  // open: clr
  and and_28 (and_28_out, RegWrite, decoder_1_out23);
  Register #(.width(32)) register_13 (.D(BusW), .en(and_13_out), .Q(register_13_q), .clk(Clock));  // open: clr
  and and_29 (and_29_out, RegWrite, decoder_1_out25);
  Register #(.width(32)) register_14 (.D(BusW), .en(and_14_out), .Q(register_14_q), .clk(Clock));  // open: clr
  and and_30 (and_30_out, RegWrite, decoder_1_out27);
  Register #(.width(32)) register_15 (.D(BusW), .en(and_15_out), .Q(register_15_q), .clk(Clock));  // open: clr
  and and_31 (and_31_out, RegWrite, decoder_1_out29);
  Register #(.width(32)) register_16 (.D(BusW), .en(and_16_out), .Q(register_16_q), .clk(Clock));  // open: clr
  and and_32 (and_32_out, RegWrite, decoder_1_out31);
  Register #(.width(32)) register_17 (.D(BusW), .en(and_17_out), .Q(register_17_q), .clk(Clock));  // open: clr
  Register #(.width(32)) register_18 (.D(BusW), .en(and_18_out), .Q(register_18_q), .clk(Clock));  // open: clr
  Register #(.width(32)) register_19 (.D(BusW), .en(and_19_out), .Q(register_19_q), .clk(Clock));  // open: clr
  Register #(.width(32)) register_20 (.D(BusW), .en(and_20_out), .Q(register_20_q), .clk(Clock));  // open: clr
  Register #(.width(32)) register_21 (.D(BusW), .en(and_21_out), .Q(register_21_q), .clk(Clock));  // open: clr
  Register #(.width(32)) register_22 (.D(BusW), .en(and_22_out), .Q(register_22_q), .clk(Clock));  // open: clr
  Register #(.width(32)) register_23 (.D(BusW), .en(and_23_out), .Q(register_23_q), .clk(Clock));  // open: clr
  Register #(.width(32)) register_24 (.D(BusW), .en(and_24_out), .Q(register_24_q), .clk(Clock));  // open: clr
  Register #(.width(32)) register_25 (.D(BusW), .en(and_25_out), .Q(register_25_q), .clk(Clock));  // open: clr
  Register #(.width(32)) register_26 (.D(BusW), .en(and_26_out), .Q(register_26_q), .clk(Clock));  // open: clr
  Register #(.width(32)) register_27 (.D(BusW), .en(and_27_out), .Q(register_27_q), .clk(Clock));  // open: clr
  Register #(.width(32)) register_28 (.D(BusW), .en(and_28_out), .Q(register_28_q), .clk(Clock));  // open: clr
  Register #(.width(32)) register_29 (.D(BusW), .en(and_29_out), .Q(register_29_q), .clk(Clock));  // open: clr
  Register #(.width(32)) register_30 (.D(BusW), .en(and_30_out), .Q(register_30_q), .clk(Clock));  // open: clr
  Register #(.width(32)) register_31 (.D(BusW), .en(and_31_out), .Q(register_31_q), .clk(Clock));  // open: clr
  Register #(.width(32)) register_32 (.D(BusW), .en(and_32_out), .Q(register_32_q), .clk(Clock));  // open: clr
  Multiplexer #(.select(5), .width(32)) multiplexer_1 (
    .in0(register_1_q), .in1(register_17_q), .in2(register_2_q), .in3(register_18_q), .in4(register_3_q),
    .in5(register_19_q), .in6(register_4_q), .in7(register_20_q), .in8(register_5_q), .in9(register_21_q),
    .in10(register_6_q), .in11(register_22_q), .in12(register_7_q), .in13(register_23_q),
    .in14(register_8_q), .in15(register_24_q), .in16(register_9_q), .in17(register_25_q),
    .in18(register_10_q), .in19(register_26_q), .in20(register_11_q), .in21(register_27_q),
    .in22(register_12_q), .in23(register_28_q), .in24(register_13_q), .in25(register_29_q),
    .in26(register_14_q), .in27(register_30_q), .in28(register_15_q), .in29(register_31_q),
    .in30(register_16_q), .in31(register_32_q), .out(BusA), .sel(RA_address));
  Multiplexer #(.select(5), .width(32)) multiplexer_2 (
    .in0(register_1_q), .in1(register_17_q), .in2(register_2_q), .in3(register_18_q), .in4(register_3_q),
    .in5(register_19_q), .in6(register_4_q), .in7(register_20_q), .in8(register_5_q), .in9(register_21_q),
    .in10(register_6_q), .in11(register_22_q), .in12(register_7_q), .in13(register_23_q),
    .in14(register_8_q), .in15(register_24_q), .in16(register_9_q), .in17(register_25_q),
    .in18(register_10_q), .in19(register_26_q), .in20(register_11_q), .in21(register_27_q),
    .in22(register_12_q), .in23(register_28_q), .in24(register_13_q), .in25(register_29_q),
    .in26(register_14_q), .in27(register_30_q), .in28(register_15_q), .in29(register_31_q),
    .in30(register_16_q), .in31(register_32_q), .out(BusB), .sel(RB_address));
endmodule

module NextPc (
  input  [29:0] PC_inc,
  input  [25:0] Imm26,
  input  Beq,
  input  Bne,
  input  J,
  input  Zero,
  output [29:0] Jumped_Address,
  output PcSrc
);

  wire and_1_out, and_2_out, not_1_out;
  wire [29:0] adder_1_out, bit_extender_1_out;

  assign bit_extender_1_out = {{14{Imm26[15]}}, Imm26[15:0]};  // Bit_Extender bit_extender_1
  Adder #(.width(30)) adder_1 (.a(PC_inc), .b(bit_extender_1_out), .out(adder_1_out));  // open: cin, cout
  Multiplexer #(.width(30)) multiplexer_1 (
    .in0(adder_1_out), .in1({PC_inc[29:26], Imm26}), .out(Jumped_Address), .sel(J));
  or or_1 (PcSrc, and_1_out, J, and_2_out);
  and and_1 (and_1_out, not_1_out, Bne);
  not not_1 (not_1_out, Zero);
  and and_2 (and_2_out, Zero, Beq);

  // Other names for the same wires on the sheet: tunnel1[3:0] = PC_inc[29:26]
endmodule

module Main_Control (
  input  [5:0] OP,
  output ALUsrc,
  output ExtOp,
  output RegDst,
  output [2:0] J_Beq_Bne,
  output RegWrite,
  output MemRead,
  output MemWrite,
  output MemReg
);

  wire and_1_out, and_2_out, and_3_out, nand_1_out, nand_2_out, nand_3_out, nand_5_out, nand_6_out,
       nand_8_out, not_1_out, not_2_out, not_3_out, not_6_out, or_1_out, or_2_out, or_3_out, or_4_out,
       or_5_out, or_6_out;

  not not_1 (not_1_out, OP[4]);
  not not_2 (not_2_out, OP[2]);
  not not_3 (not_3_out, OP[0]);
  or or_1 (or_1_out, OP[4], OP[5]);
  nand nand_1 (nand_1_out, OP[3], 1'b1);
  nand nand_2 (nand_2_out, OP[1], 1'b1);
  or or_2 (or_2_out, OP[0], OP[2]);
  and and_1 (and_1_out, OP[1], OP[0]);
  or or_3 (or_3_out, OP[3], or_1_out);
  nand nand_3 (nand_3_out, OP[2], nand_2_out);
  or or_4 (or_4_out, or_1_out, or_2_out);
  and and_2 (and_2_out, and_1_out, not_2_out, OP[5], not_1_out);
  nor nor_1 (J_Beq_Bne[0], or_2_out, or_3_out, nand_2_out);
  or or_5 (or_5_out, or_3_out, or_2_out, OP[1]);
  nor nor_2 (J_Beq_Bne[1], nand_3_out, or_3_out, OP[0]);
  and and_3 (and_3_out, nand_3_out, OP[0]);
  nor nor_3 (J_Beq_Bne[2], nand_3_out, or_3_out, not_3_out);
  or or_6 (or_6_out, nand_1_out, or_1_out, and_3_out);
  nand nand_4 (RegDst, 1'b1, or_5_out);
  nand nand_5 (nand_5_out, and_2_out, OP[3]);
  nand nand_6 (nand_6_out, nand_1_out, and_2_out);
  not not_4 (MemWrite, nand_5_out);
  nand nand_7 (ExtOp, nand_5_out, or_4_out, nand_6_out);
  nand nand_8 (nand_8_out, or_6_out, nand_6_out);
  not not_5 (MemRead, nand_6_out);
  or or_7 (ALUsrc, MemWrite, nand_8_out);
  not not_6 (not_6_out, nand_8_out);
  nand nand_9 (RegWrite, or_5_out, not_6_out);

  assign MemReg = MemRead;
endmodule

module ALUctrl (
  input  [5:0] func,
  input  [5:0] OP,
  output [6:0] ALUop
);

  wire and_1_out, and_2_out, and_3_out, and_4_out, and_5_out, and_6_out, and_7_out, and_8_out, and_9_out,
       and_10_out, EN0, EN1, EN2, EN3, not_1_out, not_2_out, not_3_out, not_4_out, not_5_out, not_6_out,
       not_7_out, not_8_out, not_9_out, not_10_out, not_11_out, not_12_out, not_13_out, not_14_out,
       not_15_out, not_16_out, not_17_out;

  not not_1 (not_1_out, OP[3]);
  not not_2 (not_2_out, OP[2]);
  not not_3 (not_3_out, OP[0]);
  not not_4 (not_4_out, OP[3]);
  not not_5 (not_5_out, OP[0]);
  not not_6 (not_6_out, OP[2]);
  not not_7 (not_7_out, OP[0]);
  not not_8 (not_8_out, OP[1]);
  not not_9 (not_9_out, OP[3]);
  not not_10 (not_10_out, OP[2]);
  not not_11 (not_11_out, OP[0]);
  not not_12 (not_12_out, OP[3]);
  not not_13 (not_13_out, OP[2]);
  not not_14 (not_14_out, OP[0]);
  not not_15 (not_15_out, OP[2]);
  not not_16 (not_16_out, OP[0]);
  and and_1 (and_1_out, not_12_out, not_13_out, not_14_out, func[3]);
  and and_2 (and_2_out, not_15_out, OP[1], not_16_out);
  and and_3 (and_3_out, not_1_out, not_2_out, not_3_out, func[2]);
  and and_4 (and_4_out, OP[3], OP[2]);
  and and_5 (and_5_out, not_4_out, func[1], not_5_out);
  and and_6 (and_6_out, not_6_out, OP[1], not_7_out);
  and and_7 (and_7_out, OP[1], OP[2]);
  not not_17 (not_17_out, OP[3]);
  and and_8 (and_8_out, not_17_out, OP[2]);
  and and_9 (and_9_out, OP[3], not_8_out, OP[0]);
  and and_10 (and_10_out, not_9_out, not_10_out, not_11_out, func[0]);
  or or_1 (EN2, and_3_out, and_4_out);
  or or_2 (EN0, and_9_out, and_10_out);
  or or_3 (EN3, and_1_out, and_2_out);
  or or_4 (EN1, and_5_out, and_6_out, and_7_out, and_8_out);
  Multiplexer #(.select(4), .width(7)) multiplexer_1 (
    .in0(7'b1000000), .in2(7'b1000100), .in4(7'b1100000), .in5(7'b1101000), .in6(7'b1111000),
    .in10(7'b0100100), .out(ALUop), .sel({EN3, EN2, EN1, EN0}));  // open: in1, in3, in7, in8, in9, in11, in12, in13, in14, in15

  // Other names for the same wires on the sheet: F0 = func[0]; F1 = func[1]; F2 = func[2]; F3 = func[3]; F4 = func[4];
  //   F5 = func[5]
endmodule

module plus_one (
  input  [21:0] in_1,
  output [21:0] out_2
);

  Adder #(.width(22)) adder_1 (.a(22'h1), .b(in_1), .out(out_2));  // open: cin, cout
endmodule

module HazardDetector (
  input  [4:0] Rs,
  input  [4:0] Rd2,
  input  [4:0] Rd3,
  input  [4:0] Rd4,
  input  EX_RegWrite,
  input  MEM_RegWrite,
  input  WB_RegWrite,
  input  [4:0] Rt,
  output [1:0] ForwardA,
  output [1:0] ForwardB
);

  wire and_1_out, and_2_out, and_3_out, and_4_out, and_5_out, and_6_out, comparator_1_eq, comparator_2_eq,
       comparator_3_eq, comparator_4_eq, comparator_5_eq, comparator_6_eq, comparator_7_eq, comparator_8_eq,
       not_1_out, not_2_out;
  wire [1:0] multiplexer_1_out, multiplexer_2_out, multiplexer_3_out, multiplexer_4_out, multiplexer_5_out,
       multiplexer_7_out;

  not not_1 (not_1_out, comparator_1_eq);
  Comparator #(.width(5)) comparator_1 (.a(Rs), .b({5{1'b0}}), .eq(comparator_1_eq));  // open: gt, lt
  Comparator #(.width(5)) comparator_2 (.a(Rs), .b(Rd2), .eq(comparator_2_eq));  // open: gt, lt
  Comparator #(.width(5)) comparator_3 (.a(Rs), .b(Rd3), .eq(comparator_3_eq));  // open: gt, lt
  Comparator #(.width(5)) comparator_4 (.a(Rs), .b(Rd4), .eq(comparator_4_eq));  // open: gt, lt
  Comparator #(.width(5)) comparator_5 (.a(Rt), .b({5{1'b0}}), .eq(comparator_5_eq));  // open: gt, lt
  Comparator #(.width(5)) comparator_6 (.a(Rt), .b(Rd2), .eq(comparator_6_eq));  // open: gt, lt
  Comparator #(.width(5)) comparator_7 (.a(Rt), .b(Rd3), .eq(comparator_7_eq));  // open: gt, lt
  Comparator #(.width(5)) comparator_8 (.a(Rt), .b(Rd4), .eq(comparator_8_eq));  // open: gt, lt
  not not_2 (not_2_out, comparator_5_eq);
  and and_1 (and_1_out, comparator_2_eq, EX_RegWrite);
  and and_2 (and_2_out, comparator_3_eq, MEM_RegWrite);
  and and_3 (and_3_out, comparator_4_eq, WB_RegWrite);
  and and_4 (and_4_out, comparator_6_eq, EX_RegWrite);
  and and_5 (and_5_out, comparator_7_eq, MEM_RegWrite);
  and and_6 (and_6_out, comparator_8_eq, WB_RegWrite);
  Multiplexer #(.width(2)) multiplexer_1 (
    .in0(multiplexer_2_out), .in1(2'b10), .out(multiplexer_1_out), .sel(and_2_out));
  Multiplexer #(.width(2)) multiplexer_2 (.in0(2'b00), .in1(2'b11), .out(multiplexer_2_out), .sel(and_3_out));
  Multiplexer #(.width(2)) multiplexer_3 (
    .in0(multiplexer_1_out), .in1(2'b01), .out(multiplexer_3_out), .sel(and_1_out));
  Multiplexer #(.width(2)) multiplexer_4 (
    .in0(multiplexer_5_out), .in1(2'b10), .out(multiplexer_4_out), .sel(and_5_out));
  Multiplexer #(.width(2)) multiplexer_5 (.in0(2'b00), .in1(2'b11), .out(multiplexer_5_out), .sel(and_6_out));
  Multiplexer #(.width(2)) multiplexer_6 (.in0(2'b00), .in1(multiplexer_3_out), .out(ForwardA), .sel(not_1_out));
  Multiplexer #(.width(2)) multiplexer_7 (
    .in0(multiplexer_4_out), .in1(2'b01), .out(multiplexer_7_out), .sel(and_4_out));
  Multiplexer #(.width(2)) multiplexer_8 (.in0(2'b00), .in1(multiplexer_7_out), .out(ForwardB), .sel(not_2_out));
endmodule
