// Logisim project MIPS_Pipeline_NoInc.circ as structural Verilog: 19 circuits, main circuit MIPS
// Reg
module Regisiters (
  input  Clk,
  input  [4:0] RA,
  input  [4:0] RB,
  input  [31:0] BusW,
  input  EnableWrite,
  input  [4:0] RW,
  output [31:0] disp1,
  output [31:0] disp2,
  output [31:0] disp3,
  output [31:0] disp4,
  output [31:0] BusA,
  output [31:0] BusB
);

  wire and_1_out, and_2_out, and_3_out, and_4_out, and_5_out, and_6_out, and_7_out, and_8_out, and_9_out,
       and_10_out, and_11_out, and_12_out, and_13_out, and_14_out, and_15_out, and_16_out, and_17_out,
       and_18_out, and_19_out, and_20_out, and_21_out, and_22_out, and_23_out, and_24_out, and_25_out,
       and_26_out, and_27_out, and_28_out, and_29_out, and_30_out, and_31_out, decoder_1_out1,
       decoder_1_out2, decoder_1_out3, decoder_1_out4, decoder_1_out5, decoder_1_out6, decoder_1_out7,
       decoder_1_out8, decoder_1_out9, decoder_1_out10, decoder_1_out11, decoder_1_out12, decoder_1_out13,
       decoder_1_out14, decoder_1_out15, decoder_1_out16, decoder_1_out17, decoder_1_out18, decoder_1_out19,
       decoder_1_out20, decoder_1_out21, decoder_1_out22, decoder_1_out23, decoder_1_out24, decoder_1_out25,
       decoder_1_out26, decoder_1_out27, decoder_1_out28, decoder_1_out29, decoder_1_out30, decoder_1_out31,
       decoder_2_out0, decoder_2_out1, decoder_2_out2, decoder_2_out3, decoder_2_out4, decoder_2_out5,
       decoder_2_out6, decoder_2_out7, decoder_2_out8, decoder_2_out9, decoder_2_out10, decoder_2_out11,
       decoder_2_out12, decoder_2_out13, decoder_2_out14, decoder_2_out15, decoder_2_out16, decoder_2_out17,
       decoder_2_out18, decoder_2_out19, decoder_2_out20, decoder_2_out21, decoder_2_out22, decoder_2_out23,
       decoder_2_out24, decoder_2_out25, decoder_2_out26, decoder_2_out27, decoder_2_out28, decoder_2_out29,
       decoder_2_out30, decoder_2_out31, decoder_3_out0, decoder_3_out1, decoder_3_out2, decoder_3_out3,
       decoder_3_out4, decoder_3_out5, decoder_3_out6, decoder_3_out7, decoder_3_out8, decoder_3_out9,
       decoder_3_out10, decoder_3_out11, decoder_3_out12, decoder_3_out13, decoder_3_out14, decoder_3_out15,
       decoder_3_out16, decoder_3_out17, decoder_3_out18, decoder_3_out19, decoder_3_out20, decoder_3_out21,
       decoder_3_out22, decoder_3_out23, decoder_3_out24, decoder_3_out25, decoder_3_out26, decoder_3_out27,
       decoder_3_out28, decoder_3_out29, decoder_3_out30, decoder_3_out31;
  wire [31:0] R0_q, R1_q, R2_q, R3_q, R4_q, R5_q, R6_q, R7_q, R12_q, R13_q, R14_q, R15_q, R16_q, R17_q,
       R18_q, R19_q, R20_q, R21_q, R22_q, R23_q, R24_q, R25_q, R26_q, R27_q, R28_q, R29_q, R30_q, R31_q;

  Decoder #(.enable("false"), .select(5)) decoder_1 (
    .out1(decoder_1_out1), .out2(decoder_1_out2), .out3(decoder_1_out3), .out4(decoder_1_out4),
    .out5(decoder_1_out5), .out6(decoder_1_out6), .out7(decoder_1_out7), .out8(decoder_1_out8),
    .out9(decoder_1_out9), .out10(decoder_1_out10), .out11(decoder_1_out11), .out12(decoder_1_out12),
    .out13(decoder_1_out13), .out14(decoder_1_out14), .out15(decoder_1_out15), .out16(decoder_1_out16),
    .out17(decoder_1_out17), .out18(decoder_1_out18), .out19(decoder_1_out19), .out20(decoder_1_out20),
    .out21(decoder_1_out21), .out22(decoder_1_out22), .out23(decoder_1_out23), .out24(decoder_1_out24),
    .out25(decoder_1_out25), .out26(decoder_1_out26), .out27(decoder_1_out27), .out28(decoder_1_out28),
    .out29(decoder_1_out29), .out30(decoder_1_out30), .out31(decoder_1_out31), .sel(RW));  // open: out0
  and and_1 (and_1_out, EnableWrite, decoder_1_out1);
  and and_2 (and_2_out, EnableWrite, decoder_1_out2);
  and and_3 (and_3_out, EnableWrite, decoder_1_out3);
  and and_4 (and_4_out, EnableWrite, decoder_1_out4);
  and and_5 (and_5_out, EnableWrite, decoder_1_out5);
  and and_6 (and_6_out, EnableWrite, decoder_1_out6);
  and and_7 (and_7_out, EnableWrite, decoder_1_out7);
  and and_8 (and_8_out, EnableWrite, decoder_1_out8);
  and and_9 (and_9_out, EnableWrite, decoder_1_out9);
  and and_10 (and_10_out, EnableWrite, decoder_1_out10);
  and and_11 (and_11_out, EnableWrite, decoder_1_out11);
  and and_12 (and_12_out, EnableWrite, decoder_1_out12);
  and and_13 (and_13_out, EnableWrite, decoder_1_out13);
  and and_14 (and_14_out, EnableWrite, decoder_1_out14);
  and and_15 (and_15_out, EnableWrite, decoder_1_out15);
  and and_16 (and_16_out, EnableWrite, decoder_1_out16);
  and and_17 (and_17_out, EnableWrite, decoder_1_out17);
  and and_18 (and_18_out, EnableWrite, decoder_1_out18);
  and and_19 (and_19_out, EnableWrite, decoder_1_out19);
  and and_20 (and_20_out, EnableWrite, decoder_1_out20);
  and and_21 (and_21_out, EnableWrite, decoder_1_out21);
  and and_22 (and_22_out, EnableWrite, decoder_1_out22);
  and and_23 (and_23_out, EnableWrite, decoder_1_out23);
  and and_24 (and_24_out, EnableWrite, decoder_1_out24);
  and and_25 (and_25_out, EnableWrite, decoder_1_out25);
  and and_26 (and_26_out, EnableWrite, decoder_1_out26);
  and and_27 (and_27_out, EnableWrite, decoder_1_out27);
  and and_28 (and_28_out, EnableWrite, decoder_1_out28);
  and and_29 (and_29_out, EnableWrite, decoder_1_out29);
  and and_30 (and_30_out, EnableWrite, decoder_1_out30);
  and and_31 (and_31_out, EnableWrite, decoder_1_out31);
  Register #(.width(32)) R0 (.D({32{1'b0}}), .en(1'b1), .clk(Clk), .Q(R0_q));  // open: clr
  Register #(.width(32)) R1 (.D(BusW), .en(and_1_out), .clk(Clk), .Q(R1_q));  // open: clr
  Register #(.width(32)) R2 (.D(BusW), .en(and_2_out), .clk(Clk), .Q(R2_q));  // open: clr
  Register #(.width(32)) R3 (.D(BusW), .en(and_3_out), .clk(Clk), .Q(R3_q));  // open: clr
  Register #(.width(32)) R4 (.D(BusW), .en(and_4_out), .clk(Clk), .Q(R4_q));  // open: clr
  Register #(.width(32)) R5 (.D(BusW), .en(and_5_out), .clk(Clk), .Q(R5_q));  // open: clr
  Register #(.width(32)) R6 (.D(BusW), .en(and_6_out), .clk(Clk), .Q(R6_q));  // open: clr
  Register #(.width(32)) R7 (.D(BusW), .en(and_7_out), .clk(Clk), .Q(R7_q));  // open: clr
  Register #(.width(32)) R8 (.D(BusW), .en(and_8_out), .clk(Clk), .Q(disp1));  // open: clr
  Register #(.width(32)) R9 (.D(BusW), .en(and_9_out), .clk(Clk), .Q(disp2));  // open: clr
  Register #(.width(32)) R10 (.D(BusW), .en(and_10_out), .clk(Clk), .Q(disp3));  // open: clr
  Register #(.width(32)) R11 (.D(BusW), .en(and_11_out), .clk(Clk), .Q(disp4));  // open: clr
  Register #(.width(32)) R12 (.D(BusW), .en(and_12_out), .clk(Clk), .Q(R12_q));  // open: clr
  Register #(.width(32)) R13 (.D(BusW), .en(and_13_out), .clk(Clk), .Q(R13_q));  // open: clr
  Register #(.width(32)) R14 (.D(BusW), .en(and_14_out), .clk(Clk), .Q(R14_q));  // open: clr
  Register #(.width(32)) R15 (.D(BusW), .en(and_15_out), .clk(Clk), .Q(R15_q));  // open: clr
  Register #(.width(32)) R16 (.D(BusW), .en(and_16_out), .clk(Clk), .Q(R16_q));  // open: clr
  Register #(.width(32)) R17 (.D(BusW), .en(and_17_out), .clk(Clk), .Q(R17_q));  // open: clr
  Register #(.width(32)) R18 (.D(BusW), .en(and_18_out), .clk(Clk), .Q(R18_q));  // open: clr
  Register #(.width(32)) R19 (.D(BusW), .en(and_19_out), .clk(Clk), .Q(R19_q));  // open: clr
  Register #(.width(32)) R20 (.D(BusW), .en(and_20_out), .clk(Clk), .Q(R20_q));  // open: clr
  Register #(.width(32)) R21 (.D(BusW), .en(and_21_out), .clk(Clk), .Q(R21_q));  // open: clr
  Register #(.width(32)) R22 (.D(BusW), .en(and_22_out), .clk(Clk), .Q(R22_q));  // open: clr
  Register #(.width(32)) R23 (.D(BusW), .en(and_23_out), .clk(Clk), .Q(R23_q));  // open: clr
  Register #(.width(32)) R24 (.D(BusW), .en(and_24_out), .clk(Clk), .Q(R24_q));  // open: clr
  Register #(.width(32)) R25 (.D(BusW), .en(and_25_out), .clk(Clk), .Q(R25_q));  // open: clr
  Register #(.width(32)) R26 (.D(BusW), .en(and_26_out), .clk(Clk), .Q(R26_q));  // open: clr
  Register #(.width(32)) R27 (.D(BusW), .en(and_27_out), .clk(Clk), .Q(R27_q));  // open: clr
  Register #(.width(32)) R28 (.D(BusW), .en(and_28_out), .clk(Clk), .Q(R28_q));  // open: clr
  Register #(.width(32)) R29 (.D(BusW), .en(and_29_out), .clk(Clk), .Q(R29_q));  // open: clr
  Register #(.width(32)) R30 (.D(BusW), .en(and_30_out), .clk(Clk), .Q(R30_q));  // open: clr
  Register #(.width(32)) R31 (.D(BusW), .en(and_31_out), .clk(Clk), .Q(R31_q));  // open: clr
  Decoder #(.enable("false"), .select(5)) decoder_2 (
    .out0(decoder_2_out0), .out1(decoder_2_out1), .out2(decoder_2_out2), .out3(decoder_2_out3),
    .out4(decoder_2_out4), .out5(decoder_2_out5), .out6(decoder_2_out6), .out7(decoder_2_out7),
    .out8(decoder_2_out8), .out9(decoder_2_out9), .out10(decoder_2_out10), .out11(decoder_2_out11),
    .out12(decoder_2_out12), .out13(decoder_2_out13), .out14(decoder_2_out14), .out15(decoder_2_out15),
    .out16(decoder_2_out16), .out17(decoder_2_out17), .out18(decoder_2_out18), .out19(decoder_2_out19),
    .out20(decoder_2_out20), .out21(decoder_2_out21), .out22(decoder_2_out22), .out23(decoder_2_out23),
    .out24(decoder_2_out24), .out25(decoder_2_out25), .out26(decoder_2_out26), .out27(decoder_2_out27),
    .out28(decoder_2_out28), .out29(decoder_2_out29), .out30(decoder_2_out30), .out31(decoder_2_out31),
    .sel(RA));
  assign BusA = decoder_2_out0 ? R0_q : 32'bz;  // Controlled_Buffer controlled_buffer_1
  assign BusA = decoder_2_out1 ? R1_q : 32'bz;  // Controlled_Buffer controlled_buffer_2
  assign BusA = decoder_2_out2 ? R2_q : 32'bz;  // Controlled_Buffer controlled_buffer_3
  assign BusA = decoder_2_out3 ? R3_q : 32'bz;  // Controlled_Buffer controlled_buffer_4
  assign BusA = decoder_2_out4 ? R4_q : 32'bz;  // Controlled_Buffer controlled_buffer_5
  assign BusA = decoder_2_out5 ? R5_q : 32'bz;  // Controlled_Buffer controlled_buffer_6
  assign BusA = decoder_2_out6 ? R6_q : 32'bz;  // Controlled_Buffer controlled_buffer_7
  assign BusA = decoder_2_out7 ? R7_q : 32'bz;  // Controlled_Buffer controlled_buffer_8
  assign BusA = decoder_2_out8 ? disp1 : 32'bz;  // Controlled_Buffer controlled_buffer_9
  assign BusA = decoder_2_out9 ? disp2 : 32'bz;  // Controlled_Buffer controlled_buffer_10
  assign BusA = decoder_2_out10 ? disp3 : 32'bz;  // Controlled_Buffer controlled_buffer_11
  assign BusA = decoder_2_out11 ? disp4 : 32'bz;  // Controlled_Buffer controlled_buffer_12
  assign BusA = decoder_2_out12 ? R12_q : 32'bz;  // Controlled_Buffer controlled_buffer_13
  assign BusA = decoder_2_out13 ? R13_q : 32'bz;  // Controlled_Buffer controlled_buffer_14
  assign BusA = decoder_2_out14 ? R14_q : 32'bz;  // Controlled_Buffer controlled_buffer_15
  assign BusA = decoder_2_out15 ? R15_q : 32'bz;  // Controlled_Buffer controlled_buffer_16
  assign BusA = decoder_2_out16 ? R16_q : 32'bz;  // Controlled_Buffer controlled_buffer_17
  assign BusA = decoder_2_out17 ? R17_q : 32'bz;  // Controlled_Buffer controlled_buffer_18
  assign BusA = decoder_2_out18 ? R18_q : 32'bz;  // Controlled_Buffer controlled_buffer_19
  assign BusA = decoder_2_out19 ? R19_q : 32'bz;  // Controlled_Buffer controlled_buffer_20
  assign BusA = decoder_2_out20 ? R20_q : 32'bz;  // Controlled_Buffer controlled_buffer_21
  assign BusA = decoder_2_out21 ? R21_q : 32'bz;  // Controlled_Buffer controlled_buffer_22
  assign BusA = decoder_2_out22 ? R22_q : 32'bz;  // Controlled_Buffer controlled_buffer_23
  assign BusA = decoder_2_out23 ? R23_q : 32'bz;  // Controlled_Buffer controlled_buffer_24
  assign BusA = decoder_2_out24 ? R24_q : 32'bz;  // Controlled_Buffer controlled_buffer_25
  assign BusA = decoder_2_out25 ? R25_q : 32'bz;  // Controlled_Buffer controlled_buffer_26
  assign BusA = decoder_2_out26 ? R26_q : 32'bz;  // Controlled_Buffer controlled_buffer_27
  assign BusA = decoder_2_out27 ? R27_q : 32'bz;  // Controlled_Buffer controlled_buffer_28
  assign BusA = decoder_2_out28 ? R28_q : 32'bz;  // Controlled_Buffer controlled_buffer_29
  assign BusA = decoder_2_out29 ? R29_q : 32'bz;  // Controlled_Buffer controlled_buffer_30
  assign BusA = decoder_2_out30 ? R30_q : 32'bz;  // Controlled_Buffer controlled_buffer_31
  assign BusA = decoder_2_out31 ? R31_q : 32'bz;  // Controlled_Buffer controlled_buffer_32
  Decoder #(.enable("false"), .select(5)) decoder_3 (
    .out0(decoder_3_out0), .out1(decoder_3_out1), .out2(decoder_3_out2), .out3(decoder_3_out3),
    .out4(decoder_3_out4), .out5(decoder_3_out5), .out6(decoder_3_out6), .out7(decoder_3_out7),
    .out8(decoder_3_out8), .out9(decoder_3_out9), .out10(decoder_3_out10), .out11(decoder_3_out11),
    .out12(decoder_3_out12), .out13(decoder_3_out13), .out14(decoder_3_out14), .out15(decoder_3_out15),
    .out16(decoder_3_out16), .out17(decoder_3_out17), .out18(decoder_3_out18), .out19(decoder_3_out19),
    .out20(decoder_3_out20), .out21(decoder_3_out21), .out22(decoder_3_out22), .out23(decoder_3_out23),
    .out24(decoder_3_out24), .out25(decoder_3_out25), .out26(decoder_3_out26), .out27(decoder_3_out27),
    .out28(decoder_3_out28), .out29(decoder_3_out29), .out30(decoder_3_out30), .out31(decoder_3_out31),
    .sel(RB));
  assign BusB = decoder_3_out0 ? R0_q : 32'bz;  // Controlled_Buffer controlled_buffer_33
  assign BusB = decoder_3_out1 ? R1_q : 32'bz;  // Controlled_Buffer controlled_buffer_34
  assign BusB = decoder_3_out2 ? R2_q : 32'bz;  // Controlled_Buffer controlled_buffer_35
  assign BusB = decoder_3_out3 ? R3_q : 32'bz;  // Controlled_Buffer controlled_buffer_36
  assign BusB = decoder_3_out4 ? R4_q : 32'bz;  // Controlled_Buffer controlled_buffer_37
  assign BusB = decoder_3_out5 ? R5_q : 32'bz;  // Controlled_Buffer controlled_buffer_38
  assign BusB = decoder_3_out6 ? R6_q : 32'bz;  // Controlled_Buffer controlled_buffer_39
  assign BusB = decoder_3_out7 ? R7_q : 32'bz;  // Controlled_Buffer controlled_buffer_40
  assign BusB = decoder_3_out8 ? disp1 : 32'bz;  // Controlled_Buffer controlled_buffer_41
  assign BusB = decoder_3_out9 ? disp2 : 32'bz;  // Controlled_Buffer controlled_buffer_42
  assign BusB = decoder_3_out10 ? disp3 : 32'bz;  // Controlled_Buffer controlled_buffer_43
  assign BusB = decoder_3_out11 ? disp4 : 32'bz;  // Controlled_Buffer controlled_buffer_44
  assign BusB = decoder_3_out12 ? R12_q : 32'bz;  // Controlled_Buffer controlled_buffer_45
  assign BusB = decoder_3_out13 ? R13_q : 32'bz;  // Controlled_Buffer controlled_buffer_46
  assign BusB = decoder_3_out14 ? R14_q : 32'bz;  // Controlled_Buffer controlled_buffer_47
  assign BusB = decoder_3_out15 ? R15_q : 32'bz;  // Controlled_Buffer controlled_buffer_48
  assign BusB = decoder_3_out16 ? R16_q : 32'bz;  // Controlled_Buffer controlled_buffer_49
  assign BusB = decoder_3_out17 ? R17_q : 32'bz;  // Controlled_Buffer controlled_buffer_50
  assign BusB = decoder_3_out18 ? R18_q : 32'bz;  // Controlled_Buffer controlled_buffer_51
  assign BusB = decoder_3_out19 ? R19_q : 32'bz;  // Controlled_Buffer controlled_buffer_52
  assign BusB = decoder_3_out20 ? R20_q : 32'bz;  // Controlled_Buffer controlled_buffer_53
  assign BusB = decoder_3_out21 ? R21_q : 32'bz;  // Controlled_Buffer controlled_buffer_54
  assign BusB = decoder_3_out22 ? R22_q : 32'bz;  // Controlled_Buffer controlled_buffer_55
  assign BusB = decoder_3_out23 ? R23_q : 32'bz;  // Controlled_Buffer controlled_buffer_56
  assign BusB = decoder_3_out24 ? R24_q : 32'bz;  // Controlled_Buffer controlled_buffer_57
  assign BusB = decoder_3_out25 ? R25_q : 32'bz;  // Controlled_Buffer controlled_buffer_58
  assign BusB = decoder_3_out26 ? R26_q : 32'bz;  // Controlled_Buffer controlled_buffer_59
  assign BusB = decoder_3_out27 ? R27_q : 32'bz;  // Controlled_Buffer controlled_buffer_60
  assign BusB = decoder_3_out28 ? R28_q : 32'bz;  // Controlled_Buffer controlled_buffer_61
  assign BusB = decoder_3_out29 ? R29_q : 32'bz;  // Controlled_Buffer controlled_buffer_62
  assign BusB = decoder_3_out30 ? R30_q : 32'bz;  // Controlled_Buffer controlled_buffer_63
  assign BusB = decoder_3_out31 ? R31_q : 32'bz;  // Controlled_Buffer controlled_buffer_64

  // Other names for the same wires on the sheet: RegWrite = EnableWrite; t0[31:0] = disp1; t1[31:0] = disp2;
  //   t2[31:0] = disp3; t3[31:0] = disp4

  // Notes on the sheet:
  //   $t0
  //   $t1
  //   $t2
  //   $t3
endmodule

module Shifter (
  input  [4:0] ShiftVal,
  input  [31:0] Data,
  input  [1:0] ShiftOp,
  output [31:0] Data_Out
);

  wire EnableSLL;
  wire [4:0] bit_extender_1_out, xor_1_out;
  wire [32:0] multiplexer_5_out;
  wire [34:0] multiplexer_4_out;
  wire [38:0] multiplexer_3_out;
  wire [46:0] multiplexer_1_out, multiplexer_2_out;
  wire [46:31] multiplexer_1_out_2;
  wire [62:0] bit_extender_2_out, bit_extender_3_out;

  assign bit_extender_1_out = {{4{EnableSLL}}, EnableSLL};  // Bit_Extender bit_extender_1
  assign xor_1_out = ShiftVal ^ bit_extender_1_out;  // XOR_Gate xor_1, 5 bits wide
  nor nor_1 (EnableSLL, ShiftOp[0], ShiftOp[1]);
  assign bit_extender_2_out = {{31{1'b0}}, Data};  // Bit_Extender bit_extender_2
  assign bit_extender_3_out = {{31{Data[31]}}, Data};  // Bit_Extender bit_extender_3
  Multiplexer #(.select(2), .width(63)) multiplexer_1 (
    .in0({Data, {31{1'b0}}}), .in1(bit_extender_2_out), .in2(bit_extender_3_out), .in3({Data[30:0], Data}),
    .out({multiplexer_1_out_2, multiplexer_1_out}), .sel(ShiftOp));
  Multiplexer #(.width(47)) multiplexer_2 (
    .in0(multiplexer_1_out), .in1({multiplexer_1_out_2, multiplexer_1_out[46:16]}), .out(multiplexer_2_out),
    .sel(xor_1_out[4]));
  Multiplexer #(.width(39)) multiplexer_3 (
    .in0(multiplexer_2_out[38:0]), .in1(multiplexer_2_out[46:8]), .out(multiplexer_3_out), .sel(xor_1_out[3]));
  Multiplexer #(.width(35)) multiplexer_4 (
    .in0(multiplexer_3_out[34:0]), .in1(multiplexer_3_out[38:4]), .out(multiplexer_4_out), .sel(xor_1_out[2]));
  Multiplexer #(.width(33)) multiplexer_5 (
    .in0(multiplexer_4_out[32:0]), .in1(multiplexer_4_out[34:2]), .out(multiplexer_5_out), .sel(xor_1_out[1]));
  Multiplexer #(.width(32)) multiplexer_6 (
    .in0(multiplexer_5_out[31:0]), .in1(multiplexer_5_out[32:1]), .out(Data_Out), .sel(xor_1_out[0]));

  // Notes on the sheet:
  //   SLL = 00
  //   SRL = 01
  //   SRA = 10
  //   ROR = 11
endmodule

module Sign (
  input  Data,
  input  Overflow,
  output [31:0] Data_Out
);

  wire xor_1_out;

  xor xor_1 (xor_1_out, Data, Overflow);
  assign Data_Out = {{31{1'b0}}, xor_1_out};  // Bit_Extender bit_extender_1
endmodule

module Instruction_Memory (
  input  [31:0] Address,
  output [31:0] Instruction
);

  ROM #(.addrWidth(24), .dataWidth(32)) ROM_1 (.addr(Address[23:0]), .data(Instruction));

  // Notes on the sheet:
  //   contents of ROM_1 (hex, n*v repeats v):
  //   4194304*0 1004024 0 0 0 1204824 0 0 0 1405024 0 0 0 1605824 0 0 0 20080004 0 0 0 2009000a 0 0 0
  //   200a0008 0 0 0 200b0002 0 0 0 ad090000 0 0 0 ad2a0008 0 0 0 8d110000 0 0 0 8e320008 0 0 0 24b1020 0
  //   0 0 ac02000c 0 0 0 2421822 0 0 0 ac030010
endmodule

module Data_Memory (
  input  [31:0] Address,
  input  [31:0] Data_in,
  input  MemStore,
  input  MemLoad,
  input  Clk,
  output [31:0] Data_out
);

  RAM #(.addrWidth(16), .asyncread("true"), .dataWidth(32)) RAM_1 (
    .addr(Address[15:0]), .we(MemStore), .oe(MemLoad), .clk(Clk), .din(Data_in), .dout(Data_out));
endmodule

module Next_PC (
  input  [29:0] incPC,
  input  [25:0] imm26,
  input  Zero,
  input  Bne,
  input  J,
  input  Beq,
  output [29:0] PCaddress,
  output PCSrc
);

  wire and_1_out, and_2_out, not_1_out;
  wire [29:0] adder_1_out, bit_extender_1_out;

  assign bit_extender_1_out = {{14{imm26[15]}}, imm26[15:0]};  // Bit_Extender bit_extender_1
  Adder #(.width(30)) adder_1 (.a(incPC), .b(bit_extender_1_out), .out(adder_1_out));  // open: cin, cout
  not not_1 (not_1_out, Zero);
  and and_1 (and_1_out, not_1_out, Bne);
  and and_2 (and_2_out, Zero, Beq);
  Multiplexer #(.width(30)) multiplexer_1 (.in0(adder_1_out), .in1({incPC[29:26], imm26}), .out(PCaddress), .sel(J));
  or or_1 (PCSrc, and_1_out, J, and_2_out);

  // Other names for the same wires on the sheet: msb4[3:0] = incPC[29:26]
endmodule

module ALU (
  input  [31:0] BusA,
  input  [31:0] BusB,
  input  [3:0] ALUCtrl,
  output Zero,
  output [31:0] BusW
);

  wire adder_1_cout, comparator_1_lt;
  wire [31:0] adder_1_out, and_1_out, bit_extender_1_out, bit_extender_2_out, multiplexer_1_out, nor_1_out,
       or_1_out, Shitfer_data_out, SLT_data_out, xor_1_out, xor_2_out;

  assign and_1_out = BusA & BusB;  // AND_Gate and_1, 32 bits wide
  assign or_1_out = BusA | BusB;  // OR_Gate or_1, 32 bits wide
  assign xor_1_out = BusA ^ BusB;  // XOR_Gate xor_1, 32 bits wide
  assign nor_1_out = ~(BusA | BusB);  // NOR_Gate nor_1, 32 bits wide
  assign bit_extender_1_out = {{31{ALUCtrl[1]}}, ALUCtrl[1]};  // Bit_Extender bit_extender_1
  Multiplexer #(.select(2), .width(32)) multiplexer_1 (
    .in0(and_1_out), .in1(or_1_out), .in2(xor_1_out), .in3(nor_1_out), .out(multiplexer_1_out),
    .sel(ALUCtrl[1:0]));
  assign xor_2_out = BusB ^ bit_extender_1_out;  // XOR_Gate xor_2, 32 bits wide
  Adder #(.width(32)) adder_1 (.a(BusA), .b(xor_2_out), .out(adder_1_out), .cin(ALUCtrl[1]), .cout(adder_1_cout));
  Shifter Shitfer (.ShiftVal(BusA[4:0]), .Data(BusB), .ShiftOp(ALUCtrl[1:0]), .Data_Out(Shitfer_data_out));
  Sign SLT (.Data(adder_1_out[31]), .Overflow(adder_1_cout), .Data_Out(SLT_data_out));
  Comparator #(.width(32)) comparator_1 (.a(BusA), .b(BusB), .lt(comparator_1_lt));  // open: gt, eq
  assign bit_extender_2_out = {{31{1'b0}}, comparator_1_lt};  // Bit_Extender bit_extender_2
  Multiplexer #(.select(2), .width(32)) multiplexer_2 (
    .in0(adder_1_out), .in1(multiplexer_1_out), .in2(bit_extender_2_out), .in3(Shitfer_data_out), .out(BusW),
    .sel(ALUCtrl[3:2]));
  Comparator #(.width(32)) comparator_2 (.a({32{1'b0}}), .b(BusW), .eq(Zero));  // open: gt, lt

  // Other names for the same wires on the sheet: LogicOp[1:0] = ALUCtrl[1:0]; ShiftOp[1:0] = ALUCtrl[1:0];
  //   ArithOp = ALUCtrl[1]; ALUselector[1:0] = ALUCtrl[3:2]

  // Notes on the sheet:
  //   ADD = 0
  //   SUB = 1
  //   SLL = 00
  //   SRL = 01
  //   SRA = 10
  //   ROR = 11
  //   Logic
  //   AND = 00
  //   OR = 01
  //   XOR = 10
  //   NOR = 11
  //   ALU
  //    !=
  //   Arith = 00
  //   Logic = 01
  //   SLT = 10
  //   Shift = 11
endmodule

module MIPS (
);

  wire ALUSrc, ALUSrc_S2, Beq, Beq_S2, Bne, Bne_S2, Clk, comparator_1_eq, ExtOp, ExtOp_S2, J, J_S2, MemRead,
       MemRead_S2, MemRead_S3, MemToReg, MemToReg_S2, MemToReg_S3, MemWrite, MemWrite_S2, MemWrite_S3, PCSrc,
       RegDst, RegW, RegW_S2, RegW_S3, RegW_S4, Reset_out, Stall, Zero;
  wire [1:0] forwardA, forwardB;
  wire [3:0] ALU_Control_1_aluctrl, ALUCtrl, ALUCtrl_S2;
  wire [4:0] Rd, Rds2, Rds3, Rds4, Rs, Rt, RW, shamt;
  wire [5:0] funct, OpCode;
  wire [12:4] Main_Control_1_regw;
  wire [15:0] imm16;
  wire [17:0] adder_1_out, multiplexer_1_out, multiplexer_2_out, PCaddress;
  wire [19:2] disp3;
  wire [25:16] Stage2_imm;
  wire [29:0] bit_extender_1_out, bit_extender_2_out, Stage1_npc1, Stage2_npc2;
  wire [29:18] NextAddress_pcaddress;
  wire [31:0] ALU_Res, BusW, Data_in, disp1, disp2, disp4, Extenderr_imm32, mem_res, multiplexer_5_out,
       multiplexer_6_out, multiplexer_7_out, RAM_data_out, Regisiters_1_busa, Regisiters_1_busb,
       Regisiters_1_disp3, ROM_1_data, Stage2_a, Stage3_aluout, Stage3_d;

  Multiplexer #(.width(18)) multiplexer_1 (.in0(adder_1_out), .in1(PCaddress), .out(multiplexer_1_out));  // open: sel
  Register #(.width(18)) PC (.D(multiplexer_1_out), .en(1'b1), .clk(Clk), .Q(disp3), .clr(Reset_out));
  Button Reset (.out(Reset_out));
  Clock clock_1 (.out(Clk));
  Multiplexer #(.width(18)) multiplexer_2 (.in0(18'h1), .in1({18{1'b0}}), .out(multiplexer_2_out), .sel(Stall));
  Adder #(.width(18)) adder_1 (.a(multiplexer_2_out), .b(disp3), .out(adder_1_out));  // open: cin, cout
  assign bit_extender_1_out = {{12{disp3[19]}}, disp3};  // Bit_Extender bit_extender_1
  ROM #(.addrWidth(24), .dataWidth(32)) ROM_1 (.addr({4'b0100, disp3, 2'b00}), .data(ROM_1_data));
  assign bit_extender_2_out = {{12{adder_1_out[17]}}, adder_1_out};  // Bit_Extender bit_extender_2
  IF_ID Stage1 (
    .NPC(bit_extender_2_out), .Stage_reset(PCSrc), .Instruction(ROM_1_data), .Clk(Clk), .NPC1(Stage1_npc1),
    .Instruction1({OpCode, Rs, Rt, Rd, shamt, funct}));  // open: opcode, OP
  ALU_Control ALU_Control_1 (.Funct(funct), .OpCode(OpCode), .ALUCtrl(ALU_Control_1_aluctrl));
  Main_Control Main_Control_1 (
    .OpCode(OpCode), .RegDst(RegDst), .RegW(Main_Control_1_regw[4]), .ExtOp(Main_Control_1_regw[5]),
    .ALUSrc(Main_Control_1_regw[6]), .Beq(Main_Control_1_regw[7]), .Bne(Main_Control_1_regw[8]),
    .J(Main_Control_1_regw[9]), .MemRead(Main_Control_1_regw[10]), .MemWrite(Main_Control_1_regw[11]),
    .MemToReg(Main_Control_1_regw[12]));
  Hazard_Control hazard_control_1 (
    .Rs(Rs), .Rd2(Rds3), .Rd3(Rds4), .Rd4(RW), .EX_RegWrite(RegW_S3), .MEM_RegWrite(RegW_S4),
    .WB_RegWrite(RegW), .Rt(Rt), .MEM_Read(MemRead_S3), .ForwardA(forwardA), .ForwardB(forwardB),
    .Stall(Stall));
  Multiplexer #(.width(13)) multiplexer_3 (
    .in0({Main_Control_1_regw, ALU_Control_1_aluctrl}), .in1({13{1'b0}}),
    .out({MemToReg_S2, MemWrite_S2, MemRead_S2, J_S2, Bne_S2, Beq_S2, ALUSrc_S2, ExtOp_S2, RegW_S2, ALUCtrl_S2}),
    .sel(Stall));
  Multiplexer #(.width(5)) multiplexer_4 (.in0(Rt), .in1(Rd), .out(Rds2), .sel(RegDst));
  Regisiters Regisiters_1 (
    .Clk(Clk), .RA(Rs), .RB(Rt), .BusW(BusW), .EnableWrite(RegW), .RW(RW), .disp1(disp1), .disp2(disp2),
    .disp3(Regisiters_1_disp3), .disp4(disp4), .BusA(Regisiters_1_busa), .BusB(Regisiters_1_busb));
  Multiplexer #(.select(2), .width(32)) multiplexer_5 (
    .in0(Regisiters_1_busa), .in1(ALU_Res), .in2(mem_res), .in3(BusW), .out(multiplexer_5_out), .sel(forwardA));
  Multiplexer #(.select(2), .width(32)) multiplexer_6 (
    .in0(Regisiters_1_busb), .in1(ALU_Res), .in2(mem_res), .in3(BusW), .out(multiplexer_6_out), .sel(forwardB));
  Next_PC NextAddress (
    .incPC(bit_extender_1_out), .imm26({Rs, Rt, Rd, shamt, funct}), .Zero(comparator_1_eq), .Bne(Bne_S2),
    .J(J_S2), .Beq(Beq_S2), .PCaddress({NextAddress_pcaddress, PCaddress}), .PCSrc(PCSrc));
  Comparator #(.width(32)) comparator_1 (
    .a(multiplexer_6_out), .b(multiplexer_5_out), .eq(comparator_1_eq));  // open: gt, lt
  ID_Ex Stage2 (
    .NPC1(Stage1_npc1), .imm26({Rs, Rt, Rd, shamt, funct}), .busA(multiplexer_5_out),
    .busB(multiplexer_6_out), .Rd1(Rds2), .Extop_S2(ExtOp_S2), .ALUsrs_S2(ALUSrc_S2),
    .ALUctrl_S2(ALUCtrl_S2), .Beq_S2(Beq_S2), .Bne_S2(Bne_S2), .J_S2(J_S2), .MemRead_S2(MemRead_S2),
    .MemWrite_S2(MemWrite_S2), .MemToReg_S2(MemToReg_S2), .RegW_S2(RegW_S2), .Clk(Clk), .NPC2(Stage2_npc2),
    .imm({Stage2_imm, imm16}), .A(Stage2_a), .B(Data_in), .Rd2(Rds3), .ExtOp(ExtOp), .ALUSrc(ALUSrc),
    .ALUctrl(ALUCtrl), .Beq(Beq), .Bne(Bne), .J(J), .MemRead_S3(MemRead_S3), .MemWrite_S3(MemWrite_S3),
    .MemToReg_S3(MemToReg_S3), .RegW_S3(RegW_S3));
  Extender Extenderr (.ExtOp(ExtOp), .imm16(imm16), .imm32(Extenderr_imm32));
  Multiplexer #(.width(32)) multiplexer_7 (.in0(Data_in), .in1(Extenderr_imm32), .out(multiplexer_7_out), .sel(ALUSrc));
  ALU ALV (.BusA(Stage2_a), .BusB(multiplexer_7_out), .ALUCtrl(ALUCtrl), .Zero(Zero), .BusW(ALU_Res));
  Ex_Mem Stage3 (
    .ALUData(ALU_Res), .Data(Data_in), .Rd3(Rds3), .MemRead_S3(MemRead_S3), .MemWrite_S3(MemWrite_S3),
    .MemToReg_S3(MemToReg_S3), .RegW_S3(RegW_S3), .Clk(Clk), .ALUOut(Stage3_aluout), .D(Stage3_d),
    .Rd4(Rds4), .MemRead(MemRead), .MemWrite(MemWrite), .MemToReg(MemToReg), .RegW_S4(RegW_S4));
  Hex_Digit_Display disp6 (.value(disp3[7:4]));  // open: dp
  Hex_Digit_Display disp5 (.value({disp3[3:2], 2'b00}));  // open: dp
  Hex_Digit_Display u_disp4 (.value(disp1[7:4]));  // open: dp
  Hex_Digit_Display u_disp3 (.value(disp1[3:0]));  // open: dp
  Data_Memory RAM (
    .Address(Stage3_aluout), .Data_in(Stage3_d), .MemStore(MemWrite), .MemLoad(MemRead), .Clk(Clk),
    .Data_out(RAM_data_out));
  Hex_Digit_Display u_disp2 (.value(disp2[7:4]));  // open: dp
  Hex_Digit_Display u_disp1 (.value(disp2[3:0]));  // open: dp
  Multiplexer #(.width(32)) multiplexer_8 (.in0(Stage3_aluout), .in1(RAM_data_out), .out(mem_res), .sel(MemToReg));
  Mem_WB Stage4 (.Data(mem_res), .Rd3(Rds4), .RegW_S3(RegW_S4), .Clk(Clk), .WBdata(BusW), .Rd4(RW), .RegW(RegW));

  // Notes on the sheet:
  //   Program Counter Reset Button
  //   CPU Clock
  //   increment PC by 4
  //   contents of ROM_1 (hex, n*v repeats v):
  //   4194304*0 1004024 0 0 0 1204824 0 0 0 1405024 0 0 0 1605824 0 0 0 20080004 0 0 0 2009000a 0 0 0
  //   200a0008 0 0 0 200b0002 0 0 0 ad090000 0 0 0 ad2a0008 0 0 0 8d110000 0 0 0 8e320008 0 0 0 6024 0 0 0
  //   6024 0 0 0 24b1020 0 0 0 ac02000c 0 0 0 2421822 0 0 0 ac030010
  //   bubble
  //   PC
  //   Quotient
  //   Remainder
endmodule

module Extender (
  input  ExtOp,
  input  [15:0] imm16,
  output [31:0] imm32
);

  and and_1 (imm32[31], ExtOp, imm16[15]);

  assign imm32[30:0] = {{15{imm32[31]}}, imm16};
endmodule

module Main_Control (
  input  [5:0] OpCode,
  output RegDst,
  output RegW,
  output ExtOp,
  output ALUSrc,
  output Beq,
  output Bne,
  output J,
  output MemRead,
  output MemWrite,
  output MemToReg
);

  wire addi, and_1_out, and_2_out, and_3_out, andi, not_1_out, not_2_out, not_3_out, not_4_out, not_5_out,
       not_6_out, not_7_out, not_8_out, not_9_out, not_10_out, not_11_out, not_12_out, not_13_out,
       not_14_out, not_15_out, not_16_out, not_17_out, not_18_out, or_1_out, or_2_out, or_3_out, ori, slti,
       xori;

  // Decoder_6to64 Decoder_6to64_1: pin names not known; wires that end beside it: OpCode, RegDst, J, Beq, Bne, addi, slti, andi, ori, xori, MemRead, MemWrite
  not not_1 (not_1_out, RegDst);
  not not_2 (not_2_out, addi);
  not not_3 (not_3_out, slti);
  not not_4 (not_4_out, andi);
  not not_5 (not_5_out, ori);
  not not_6 (not_6_out, xori);
  not not_7 (not_7_out, MemRead);
  not not_8 (not_8_out, addi);
  not not_9 (not_9_out, slti);
  or or_1 (or_1_out, andi, ori, xori);
  not not_10 (not_10_out, MemRead);
  not not_11 (not_11_out, MemWrite);
  not not_12 (not_12_out, MemWrite);
  not not_13 (not_13_out, addi);
  not not_14 (not_14_out, slti);
  not not_15 (not_15_out, andi);
  not not_16 (not_16_out, ori);
  not not_17 (not_17_out, xori);
  not not_18 (not_18_out, MemRead);
  or or_2 (or_2_out, MemWrite, Bne, Beq, J);
  and and_1 (and_1_out, not_8_out, not_9_out, or_1_out, not_10_out, not_11_out);
  or or_3 (or_3_out, RegDst, Bne, Beq);
  and and_2 (and_2_out, not_1_out, not_2_out, not_3_out, not_4_out, not_5_out, not_6_out, not_7_out, or_2_out);
  not not_19 (RegW, and_2_out);
  not not_20 (ExtOp, and_1_out);
  and and_3 (and_3_out, not_12_out, not_13_out, not_14_out, not_15_out, not_16_out, not_17_out, not_18_out, or_3_out);
  not not_21 (ALUSrc, and_3_out);

  assign MemToReg = MemRead;

  // Other names for the same wires on the sheet: lw = MemRead; Rtype = RegDst; sw = MemWrite
endmodule

module ALU_Control (
  input  [5:0] Funct,
  input  [5:0] OpCode,
  output [3:0] ALUCtrl
);

  wire comparator_1_eq, not_1_out;
  wire [3:0] ALU_OpCode_Decoder_6to64_1_aluctrl, funct_Decoder_6to64_1_aluctrl;

  Comparator #(.width(6)) comparator_1 (.a({6{1'b0}}), .b(OpCode), .eq(comparator_1_eq));  // open: gt, lt
  not not_1 (not_1_out, comparator_1_eq);
  ALU_OpCode_Decoder_6to64 ALU_OpCode_Decoder_6to64_1 (.OpCode(OpCode), .ALUCtrl(ALU_OpCode_Decoder_6to64_1_aluctrl));
  funct_Decoder_6to64 funct_Decoder_6to64_1 (
    .Funct(Funct), .enable(comparator_1_eq), .ALUCtrl(funct_Decoder_6to64_1_aluctrl));
  Multiplexer #(.width(4)) multiplexer_1 (
    .in0(funct_Decoder_6to64_1_aluctrl), .in1(ALU_OpCode_Decoder_6to64_1_aluctrl), .out(ALUCtrl),
    .sel(not_1_out));
endmodule

module Decoder_6to64 (
  input  [5:0] OpCode,
  output Rtype,
  output Output_1,
  output J,
  output Output_2,
  output Beq,
  output Bne,
  output Output_3,
  output Output_4,
  output addi,
  output Output_5,
  output Slti,
  output Output_6,
  output andi,
  output ori,
  output xori,
  output Output_7,
  output Output_8,
  output Output_9,
  output Output_10,
  output Output_11,
  output Output_12,
  output Output_13,
  output Output_14,
  output Output_15,
  output Output_16,
  output Output_17,
  output Output_18,
  output Output_19,
  output Output_20,
  output Output_21,
  output Output_22,
  output Output_23,
  output Output_24,
  output Output_25,
  output Output_26,
  output lw,
  output Output_27,
  output Output_28,
  output Output_29,
  output Output_30,
  output Output_31,
  output Output_32,
  output Output_33,
  output sw,
  output Output_34,
  output Output_35,
  output Output_36,
  output Output_37,
  output Output_38,
  output Output_39,
  output Output_40,
  output Output_41,
  output Output_42,
  output Output_43,
  output Output_44,
  output Output_45,
  output Output_46,
  output Output_47,
  output Output_48,
  output Output_49,
  output Output_50,
  output Output_51,
  output Output_52,
  output Output_53
);

  wire decoder_1_out0, decoder_1_out1, decoder_1_out2, decoder_1_out3, decoder_1_out4, decoder_1_out5,
       decoder_1_out6, decoder_1_out7, decoder_1_out8, decoder_1_out9, decoder_1_out10, decoder_1_out11,
       decoder_1_out12, decoder_1_out13, decoder_1_out14, decoder_1_out15, decoder_1_out16, decoder_1_out17,
       decoder_1_out18, decoder_1_out19, decoder_1_out20, decoder_1_out21, decoder_1_out22, decoder_1_out23,
       decoder_1_out24, decoder_1_out25, decoder_1_out26, decoder_1_out27, decoder_1_out28, decoder_1_out29,
       decoder_1_out30, decoder_1_out31;

  Decoder #(.enable("false"), .select(5)) decoder_1 (
    .out0(decoder_1_out0), .out1(decoder_1_out1), .out2(decoder_1_out2), .out3(decoder_1_out3),
    .out4(decoder_1_out4), .out5(decoder_1_out5), .out6(decoder_1_out6), .out7(decoder_1_out7),
    .out8(decoder_1_out8), .out9(decoder_1_out9), .out10(decoder_1_out10), .out11(decoder_1_out11),
    .out12(decoder_1_out12), .out13(decoder_1_out13), .out14(decoder_1_out14), .out15(decoder_1_out15),
    .out16(decoder_1_out16), .out17(decoder_1_out17), .out18(decoder_1_out18), .out19(decoder_1_out19),
    .out20(decoder_1_out20), .out21(decoder_1_out21), .out22(decoder_1_out22), .out23(decoder_1_out23),
    .out24(decoder_1_out24), .out25(decoder_1_out25), .out26(decoder_1_out26), .out27(decoder_1_out27),
    .out28(decoder_1_out28), .out29(decoder_1_out29), .out30(decoder_1_out30), .out31(decoder_1_out31),
    .sel(OpCode[5:1]));
  Decoder decoder_2 (.out0(Rtype), .out1(Output_1), .sel(OpCode[0]), .en(decoder_1_out0));
  Decoder decoder_3 (.out0(J), .out1(Output_2), .sel(OpCode[0]), .en(decoder_1_out1));
  Decoder decoder_4 (.out0(Beq), .out1(Bne), .sel(OpCode[0]), .en(decoder_1_out2));
  Decoder decoder_5 (.out0(Output_3), .out1(Output_4), .sel(OpCode[0]), .en(decoder_1_out3));
  Decoder decoder_6 (.out0(addi), .out1(Output_5), .sel(OpCode[0]), .en(decoder_1_out4));
  Decoder decoder_7 (.out0(Slti), .out1(Output_6), .sel(OpCode[0]), .en(decoder_1_out5));
  Decoder decoder_8 (.out0(andi), .out1(ori), .sel(OpCode[0]), .en(decoder_1_out6));
  Decoder decoder_9 (.out0(xori), .out1(Output_7), .sel(OpCode[0]), .en(decoder_1_out7));
  Decoder decoder_10 (.out0(Output_8), .out1(Output_9), .sel(OpCode[0]), .en(decoder_1_out8));
  Decoder decoder_11 (.out0(Output_10), .out1(Output_11), .sel(OpCode[0]), .en(decoder_1_out9));
  Decoder decoder_12 (.out0(Output_12), .out1(Output_13), .sel(OpCode[0]), .en(decoder_1_out10));
  Decoder decoder_13 (.out0(Output_14), .out1(Output_15), .sel(OpCode[0]), .en(decoder_1_out11));
  Decoder decoder_14 (.out0(Output_16), .out1(Output_17), .sel(OpCode[0]), .en(decoder_1_out12));
  Decoder decoder_15 (.out0(Output_18), .out1(Output_19), .sel(OpCode[0]), .en(decoder_1_out13));
  Decoder decoder_16 (.out0(Output_20), .out1(Output_21), .sel(OpCode[0]), .en(decoder_1_out14));
  Decoder decoder_17 (.out0(Output_22), .out1(Output_23), .sel(OpCode[0]), .en(decoder_1_out15));
  Decoder decoder_18 (.out0(Output_24), .out1(Output_25), .sel(OpCode[0]), .en(decoder_1_out16));
  Decoder decoder_19 (.out0(Output_26), .out1(lw), .sel(OpCode[0]), .en(decoder_1_out17));
  Decoder decoder_20 (.out0(Output_27), .out1(Output_28), .sel(OpCode[0]), .en(decoder_1_out18));
  Decoder decoder_21 (.out0(Output_29), .out1(Output_30), .sel(OpCode[0]), .en(decoder_1_out19));
  Decoder decoder_22 (.out0(Output_31), .out1(Output_32), .sel(OpCode[0]), .en(decoder_1_out20));
  Decoder decoder_23 (.out0(Output_33), .out1(sw), .sel(OpCode[0]), .en(decoder_1_out21));
  Decoder decoder_24 (.out0(Output_34), .out1(Output_35), .sel(OpCode[0]), .en(decoder_1_out22));
  Decoder decoder_25 (.out0(Output_36), .out1(Output_37), .sel(OpCode[0]), .en(decoder_1_out23));
  Decoder decoder_26 (.out0(Output_38), .out1(Output_39), .sel(OpCode[0]), .en(decoder_1_out24));
  Decoder decoder_27 (.out0(Output_40), .out1(Output_41), .sel(OpCode[0]), .en(decoder_1_out25));
  Decoder decoder_28 (.out0(Output_42), .out1(Output_43), .sel(OpCode[0]), .en(decoder_1_out26));
  Decoder decoder_29 (.out0(Output_44), .out1(Output_45), .sel(OpCode[0]), .en(decoder_1_out27));
  Decoder decoder_30 (.out0(Output_46), .out1(Output_47), .sel(OpCode[0]), .en(decoder_1_out28));
  Decoder decoder_31 (.out0(Output_48), .out1(Output_49), .sel(OpCode[0]), .en(decoder_1_out29));
  Decoder decoder_32 (.out0(Output_50), .out1(Output_51), .sel(OpCode[0]), .en(decoder_1_out30));
  Decoder decoder_33 (.out0(Output_52), .out1(Output_53), .sel(OpCode[0]), .en(decoder_1_out31));

  // Other names for the same wires on the sheet: lsb = OpCode[0]
endmodule

module funct_Decoder_6to64 (
  input  [5:0] Funct,
  input  enable,
  output [3:0] ALUCtrl
);

  wire decoder_1_out0, decoder_1_out1, decoder_1_out2, decoder_1_out3, decoder_1_out4, decoder_1_out5,
       decoder_1_out6, decoder_1_out7, decoder_1_out8, decoder_1_out9, decoder_1_out10, decoder_1_out11,
       decoder_1_out12, decoder_1_out13, decoder_1_out14, decoder_1_out15, decoder_1_out16, decoder_1_out17,
       decoder_1_out18, decoder_1_out19, decoder_1_out20, decoder_1_out21, decoder_1_out22, decoder_1_out23,
       decoder_1_out24, decoder_1_out25, decoder_1_out26, decoder_1_out27, decoder_1_out28, decoder_1_out29,
       decoder_1_out30, decoder_1_out31, decoder_2_out0, decoder_2_out1, decoder_3_out0, decoder_3_out1,
       decoder_4_out0, decoder_4_out1, decoder_5_out0, decoder_5_out1, decoder_6_out0, decoder_6_out1,
       decoder_7_out0, decoder_7_out1, decoder_8_out0, decoder_8_out1, decoder_9_out0, decoder_9_out1,
       decoder_10_out0, decoder_10_out1, decoder_11_out0, decoder_11_out1, decoder_12_out0, decoder_12_out1,
       decoder_13_out0, decoder_13_out1, decoder_14_out0, decoder_14_out1, decoder_15_out0, decoder_15_out1,
       decoder_16_out0, decoder_16_out1, decoder_17_out0, decoder_17_out1, decoder_18_out0, decoder_18_out1,
       decoder_19_out0, decoder_19_out1, decoder_20_out0, decoder_20_out1, decoder_21_out0, decoder_21_out1,
       decoder_22_out0, decoder_22_out1, decoder_23_out0, decoder_23_out1, decoder_24_out0, decoder_24_out1,
       decoder_25_out0, decoder_25_out1, decoder_26_out0, decoder_26_out1, decoder_27_out0, decoder_27_out1,
       decoder_28_out0, decoder_28_out1, decoder_29_out0, decoder_29_out1, decoder_30_out0, decoder_30_out1,
       decoder_31_out0, decoder_31_out1, decoder_32_out0, decoder_32_out1, decoder_33_out0, decoder_33_out1,
       undriven;

  Decoder #(.select(5)) decoder_1 (
    .out0(decoder_1_out0), .out1(decoder_1_out1), .out2(decoder_1_out2), .out3(decoder_1_out3),
    .out4(decoder_1_out4), .out5(decoder_1_out5), .out6(decoder_1_out6), .out7(decoder_1_out7),
    .out8(decoder_1_out8), .out9(decoder_1_out9), .out10(decoder_1_out10), .out11(decoder_1_out11),
    .out12(decoder_1_out12), .out13(decoder_1_out13), .out14(decoder_1_out14), .out15(decoder_1_out15),
    .out16(decoder_1_out16), .out17(decoder_1_out17), .out18(decoder_1_out18), .out19(decoder_1_out19),
    .out20(decoder_1_out20), .out21(decoder_1_out21), .out22(decoder_1_out22), .out23(decoder_1_out23),
    .out24(decoder_1_out24), .out25(decoder_1_out25), .out26(decoder_1_out26), .out27(decoder_1_out27),
    .out28(decoder_1_out28), .out29(decoder_1_out29), .out30(decoder_1_out30), .out31(decoder_1_out31),
    .sel(Funct[5:1]), .en(enable));
  Decoder decoder_2 (.out0(decoder_2_out0), .out1(decoder_2_out1), .sel(Funct[0]), .en(decoder_1_out0));
  Decoder decoder_3 (.out0(decoder_3_out0), .out1(decoder_3_out1), .sel(Funct[0]), .en(decoder_1_out1));
  Decoder decoder_4 (.out0(decoder_4_out0), .out1(decoder_4_out1), .sel(Funct[0]), .en(decoder_1_out2));
  Decoder decoder_5 (.out0(decoder_5_out0), .out1(decoder_5_out1), .sel(Funct[0]), .en(decoder_1_out3));
  Decoder decoder_6 (.out0(decoder_6_out0), .out1(decoder_6_out1), .sel(Funct[0]), .en(decoder_1_out4));
  Decoder decoder_7 (.out0(decoder_7_out0), .out1(decoder_7_out1), .sel(Funct[0]), .en(decoder_1_out5));
  Decoder decoder_8 (.out0(decoder_8_out0), .out1(decoder_8_out1), .sel(Funct[0]), .en(decoder_1_out6));
  Decoder decoder_9 (.out0(decoder_9_out0), .out1(decoder_9_out1), .sel(Funct[0]), .en(decoder_1_out7));
  Decoder decoder_10 (.out0(decoder_10_out0), .out1(decoder_10_out1), .sel(Funct[0]), .en(decoder_1_out8));
  Decoder decoder_11 (.out0(decoder_11_out0), .out1(decoder_11_out1), .sel(Funct[0]), .en(decoder_1_out9));
  Decoder decoder_12 (.out0(decoder_12_out0), .out1(decoder_12_out1), .sel(Funct[0]), .en(decoder_1_out10));
  Decoder decoder_13 (.out0(decoder_13_out0), .out1(decoder_13_out1), .sel(Funct[0]), .en(decoder_1_out11));
  Decoder decoder_14 (.out0(decoder_14_out0), .out1(decoder_14_out1), .sel(Funct[0]), .en(decoder_1_out12));
  Decoder decoder_15 (.out0(decoder_15_out0), .out1(decoder_15_out1), .sel(Funct[0]), .en(decoder_1_out13));
  Decoder decoder_16 (.out0(decoder_16_out0), .out1(decoder_16_out1), .sel(Funct[0]), .en(decoder_1_out14));
  Decoder decoder_17 (.out0(decoder_17_out0), .out1(decoder_17_out1), .sel(Funct[0]), .en(decoder_1_out15));
  Decoder decoder_18 (.out0(decoder_18_out0), .out1(decoder_18_out1), .sel(Funct[0]), .en(decoder_1_out16));
  Decoder decoder_19 (.out0(decoder_19_out0), .out1(decoder_19_out1), .sel(Funct[0]), .en(decoder_1_out17));
  Decoder decoder_20 (.out0(decoder_20_out0), .out1(decoder_20_out1), .sel(Funct[0]), .en(decoder_1_out18));
  Decoder decoder_21 (.out0(decoder_21_out0), .out1(decoder_21_out1), .sel(Funct[0]), .en(decoder_1_out19));
  Decoder decoder_22 (.out0(decoder_22_out0), .out1(decoder_22_out1), .sel(Funct[0]), .en(decoder_1_out20));
  Decoder decoder_23 (.out0(decoder_23_out0), .out1(decoder_23_out1), .sel(Funct[0]), .en(decoder_1_out21));
  Decoder decoder_24 (.out0(decoder_24_out0), .out1(decoder_24_out1), .sel(Funct[0]), .en(decoder_1_out22));
  Decoder decoder_25 (.out0(decoder_25_out0), .out1(decoder_25_out1), .sel(Funct[0]), .en(decoder_1_out23));
  Decoder decoder_26 (.out0(decoder_26_out0), .out1(decoder_26_out1), .sel(Funct[0]), .en(decoder_1_out24));
  Decoder decoder_27 (.out0(decoder_27_out0), .out1(decoder_27_out1), .sel(Funct[0]), .en(decoder_1_out25));
  Decoder decoder_28 (.out0(decoder_28_out0), .out1(decoder_28_out1), .sel(Funct[0]), .en(decoder_1_out26));
  Decoder decoder_29 (.out0(decoder_29_out0), .out1(decoder_29_out1), .sel(Funct[0]), .en(decoder_1_out27));
  Decoder decoder_30 (.out0(decoder_30_out0), .out1(decoder_30_out1), .sel(Funct[0]), .en(decoder_1_out28));
  Decoder decoder_31 (.out0(decoder_31_out0), .out1(decoder_31_out1), .sel(Funct[0]), .en(decoder_1_out29));
  Decoder decoder_32 (.out0(decoder_32_out0), .out1(decoder_32_out1), .sel(Funct[0]), .en(decoder_1_out30));
  Decoder decoder_33 (.out0(decoder_33_out0), .out1(decoder_33_out1), .sel(Funct[0]), .en(decoder_1_out31));
  assign ALUCtrl = decoder_18_out0 ? 4'b0000 : 4'bz;  // Controlled_Buffer controlled_buffer_1
  assign ALUCtrl = decoder_19_out0 ? 4'b0010 : 4'bz;  // Controlled_Buffer controlled_buffer_2
  assign ALUCtrl = decoder_20_out0 ? 4'b0100 : 4'bz;  // Controlled_Buffer controlled_buffer_3
  assign ALUCtrl = decoder_21_out0 ? 4'b0110 : 4'bz;  // Controlled_Buffer controlled_buffer_4
  assign ALUCtrl = decoder_23_out0 ? 4'b1010 : 4'bz;  // Controlled_Buffer controlled_buffer_5
  assign ALUCtrl = decoder_20_out1 ? 4'b0101 : 4'bz;  // Controlled_Buffer controlled_buffer_6
  Decoder decoder_34 (.en(undriven));  // open: out0, out1, sel
  Decoder decoder_35 ();  // open: out0, out1, sel, en
  Decoder decoder_36 ();  // open: out0, out1, sel, en
  Decoder decoder_37 ();  // open: out0, out1, sel, en
  Decoder decoder_38 ();  // open: out0, out1, sel, en
  Decoder decoder_39 ();  // open: out0, out1, sel, en
  Decoder decoder_40 ();  // open: out0, out1, sel, en
  Decoder decoder_41 ();  // open: out0, out1, sel, en
  Decoder decoder_42 ();  // open: out0, out1, sel, en
  Decoder decoder_43 ();  // open: out0, out1, sel, en
  Decoder decoder_44 ();  // open: out0, out1, sel, en
  Decoder decoder_45 ();  // open: out0, out1, sel, en
  Decoder decoder_46 ();  // open: out0, out1, sel, en
  Decoder decoder_47 ();  // open: out0, out1, sel, en
  Decoder decoder_48 ();  // open: out0, out1, sel, en
  Decoder decoder_49 ();  // open: out0, out1, sel, en
  Decoder decoder_50 ();  // open: out0, out1, sel, en
  Decoder decoder_51 ();  // open: out0, out1, sel, en
  Decoder decoder_52 ();  // open: out0, out1, sel, en
  Decoder decoder_53 ();  // open: out0, out1, sel, en
  Decoder decoder_54 ();  // open: out0, out1, sel, en
  Decoder decoder_55 ();  // open: out0, out1, sel, en
  Decoder decoder_56 ();  // open: out0, out1, sel, en
  Decoder decoder_57 ();  // open: out0, out1, sel, en
  Decoder decoder_58 ();  // open: out0, out1, sel, en
  Decoder decoder_59 ();  // open: out0, out1, sel, en
  Decoder decoder_60 ();  // open: out0, out1, sel, en
  Decoder decoder_61 ();  // open: out0, out1, sel, en
  Decoder decoder_62 ();  // open: out0, out1, sel, en
  Decoder decoder_63 ();  // open: out0, out1, sel, en
  Decoder decoder_64 ();  // open: out0, out1, sel, en
  Decoder decoder_65 ();  // open: out0, out1, sel, en

  // Other names for the same wires on the sheet: lsb = Funct[0]

  // Notes on the sheet:
  //   Add
  //   Sub
  //   AND
  //   XOR
  //   SLT
  //   OR
endmodule

module ALU_OpCode_Decoder_6to64 (
  input  [5:0] OpCode,
  output [3:0] ALUCtrl
);

  wire decoder_1_out0, decoder_1_out1, decoder_1_out2, decoder_1_out3, decoder_1_out4, decoder_1_out5,
       decoder_1_out6, decoder_1_out7, decoder_1_out8, decoder_1_out9, decoder_1_out10, decoder_1_out11,
       decoder_1_out12, decoder_1_out13, decoder_1_out14, decoder_1_out15, decoder_1_out16, decoder_1_out17,
       decoder_1_out18, decoder_1_out19, decoder_1_out20, decoder_1_out21, decoder_1_out22, decoder_1_out23,
       decoder_1_out24, decoder_1_out25, decoder_1_out26, decoder_1_out27, decoder_1_out28, decoder_1_out29,
       decoder_1_out30, decoder_1_out31, decoder_2_out0, decoder_2_out1, decoder_3_out0, decoder_3_out1,
       decoder_4_out0, decoder_4_out1, decoder_5_out0, decoder_5_out1, decoder_6_out0, decoder_6_out1,
       decoder_7_out0, decoder_7_out1, decoder_8_out0, decoder_8_out1, decoder_9_out0, decoder_9_out1,
       decoder_10_out0, decoder_10_out1, decoder_11_out0, decoder_11_out1, decoder_12_out0, decoder_12_out1,
       decoder_13_out0, decoder_13_out1, decoder_14_out0, decoder_14_out1, decoder_15_out0, decoder_15_out1,
       decoder_16_out0, decoder_16_out1, decoder_17_out0, decoder_17_out1, decoder_18_out0, decoder_18_out1,
       decoder_19_out0, decoder_19_out1, decoder_20_out0, decoder_20_out1, decoder_21_out0, decoder_21_out1,
       decoder_22_out0, decoder_22_out1, decoder_23_out1, decoder_24_out0, decoder_24_out1, decoder_25_out0,
       decoder_25_out1, decoder_26_out0, decoder_26_out1, decoder_27_out0, decoder_27_out1, decoder_28_out0,
       decoder_28_out1, decoder_29_out0, decoder_29_out1, decoder_30_out0, decoder_30_out1, decoder_31_out0,
       decoder_31_out1, decoder_32_out0, decoder_32_out1, decoder_33_out0, decoder_33_out1, undriven;

  Decoder #(.enable("false"), .select(5)) decoder_1 (
    .out0(decoder_1_out0), .out1(decoder_1_out1), .out2(decoder_1_out2), .out3(decoder_1_out3),
    .out4(decoder_1_out4), .out5(decoder_1_out5), .out6(decoder_1_out6), .out7(decoder_1_out7),
    .out8(decoder_1_out8), .out9(decoder_1_out9), .out10(decoder_1_out10), .out11(decoder_1_out11),
    .out12(decoder_1_out12), .out13(decoder_1_out13), .out14(decoder_1_out14), .out15(decoder_1_out15),
    .out16(decoder_1_out16), .out17(decoder_1_out17), .out18(decoder_1_out18), .out19(decoder_1_out19),
    .out20(decoder_1_out20), .out21(decoder_1_out21), .out22(decoder_1_out22), .out23(decoder_1_out23),
    .out24(decoder_1_out24), .out25(decoder_1_out25), .out26(decoder_1_out26), .out27(decoder_1_out27),
    .out28(decoder_1_out28), .out29(decoder_1_out29), .out30(decoder_1_out30), .out31(decoder_1_out31),
    .sel(OpCode[5:1]));
  Decoder decoder_2 (.out0(decoder_2_out0), .out1(decoder_2_out1), .sel(OpCode[0]), .en(decoder_1_out0));
  Decoder decoder_3 (.out0(decoder_3_out0), .out1(decoder_3_out1), .sel(OpCode[0]), .en(decoder_1_out1));
  Decoder decoder_4 (.out0(decoder_4_out0), .out1(decoder_4_out1), .sel(OpCode[0]), .en(decoder_1_out2));
  Decoder decoder_5 (.out0(decoder_5_out0), .out1(decoder_5_out1), .sel(OpCode[0]), .en(decoder_1_out3));
  Decoder decoder_6 (.out0(decoder_6_out0), .out1(decoder_6_out1), .sel(OpCode[0]), .en(decoder_1_out4));
  Decoder decoder_7 (.out0(decoder_7_out0), .out1(decoder_7_out1), .sel(OpCode[0]), .en(decoder_1_out5));
  Decoder decoder_8 (.out0(decoder_8_out0), .out1(decoder_8_out1), .sel(OpCode[0]), .en(decoder_1_out6));
  Decoder decoder_9 (.out0(decoder_9_out0), .out1(decoder_9_out1), .sel(OpCode[0]), .en(decoder_1_out7));
  Decoder decoder_10 (.out0(decoder_10_out0), .out1(decoder_10_out1), .sel(OpCode[0]), .en(decoder_1_out8));
  Decoder decoder_11 (.out0(decoder_11_out0), .out1(decoder_11_out1), .sel(OpCode[0]), .en(decoder_1_out9));
  Decoder decoder_12 (.out0(decoder_12_out0), .out1(decoder_12_out1), .sel(OpCode[0]), .en(decoder_1_out10));
  Decoder decoder_13 (.out0(decoder_13_out0), .out1(decoder_13_out1), .sel(OpCode[0]), .en(decoder_1_out11));
  Decoder decoder_14 (.out0(decoder_14_out0), .out1(decoder_14_out1), .sel(OpCode[0]), .en(decoder_1_out12));
  Decoder decoder_15 (.out0(decoder_15_out0), .out1(decoder_15_out1), .sel(OpCode[0]), .en(decoder_1_out13));
  Decoder decoder_16 (.out0(decoder_16_out0), .out1(decoder_16_out1), .sel(OpCode[0]), .en(decoder_1_out14));
  Decoder decoder_17 (.out0(decoder_17_out0), .out1(decoder_17_out1), .sel(OpCode[0]), .en(decoder_1_out15));
  Decoder decoder_18 (.out0(decoder_18_out0), .out1(decoder_18_out1), .sel(OpCode[0]), .en(decoder_1_out16));
  Decoder decoder_19 (.out0(decoder_19_out0), .out1(decoder_19_out1), .sel(OpCode[0]), .en(decoder_1_out17));
  Decoder decoder_20 (.out0(decoder_20_out0), .out1(decoder_20_out1), .sel(OpCode[0]), .en(decoder_1_out18));
  Decoder decoder_21 (.out0(decoder_21_out0), .out1(decoder_21_out1), .sel(OpCode[0]), .en(decoder_1_out19));
  Decoder decoder_22 (.out0(decoder_22_out0), .out1(decoder_22_out1), .sel(OpCode[0]), .en(decoder_1_out20));
  Decoder decoder_23 (.out1(decoder_23_out1), .sel(OpCode[0]), .en(decoder_1_out21));  // open: out0
  Decoder decoder_24 (.out0(decoder_24_out0), .out1(decoder_24_out1), .sel(OpCode[0]), .en(decoder_1_out22));
  Decoder decoder_25 (.out0(decoder_25_out0), .out1(decoder_25_out1), .sel(OpCode[0]), .en(decoder_1_out23));
  Decoder decoder_26 (.out0(decoder_26_out0), .out1(decoder_26_out1), .sel(OpCode[0]), .en(decoder_1_out24));
  Decoder decoder_27 (.out0(decoder_27_out0), .out1(decoder_27_out1), .sel(OpCode[0]), .en(decoder_1_out25));
  Decoder decoder_28 (.out0(decoder_28_out0), .out1(decoder_28_out1), .sel(OpCode[0]), .en(decoder_1_out26));
  Decoder decoder_29 (.out0(decoder_29_out0), .out1(decoder_29_out1), .sel(OpCode[0]), .en(decoder_1_out27));
  Decoder decoder_30 (.out0(decoder_30_out0), .out1(decoder_30_out1), .sel(OpCode[0]), .en(decoder_1_out28));
  Decoder decoder_31 (.out0(decoder_31_out0), .out1(decoder_31_out1), .sel(OpCode[0]), .en(decoder_1_out29));
  Decoder decoder_32 (.out0(decoder_32_out0), .out1(decoder_32_out1), .sel(OpCode[0]), .en(decoder_1_out30));
  Decoder decoder_33 (.out0(decoder_33_out0), .out1(decoder_33_out1), .sel(OpCode[0]), .en(decoder_1_out31));
  assign ALUCtrl = decoder_4_out0 ? 4'b0010 : 4'bz;  // Controlled_Buffer controlled_buffer_1
  assign ALUCtrl = decoder_6_out0 ? 4'b0000 : 4'bz;  // Controlled_Buffer controlled_buffer_2
  assign ALUCtrl = decoder_7_out0 ? 4'b1010 : 4'bz;  // Controlled_Buffer controlled_buffer_3
  assign ALUCtrl = decoder_8_out0 ? 4'b0100 : 4'bz;  // Controlled_Buffer controlled_buffer_4
  assign ALUCtrl = decoder_9_out0 ? 4'b0110 : 4'bz;  // Controlled_Buffer controlled_buffer_5
  assign ALUCtrl = decoder_19_out1 ? 4'b0000 : 4'bz;  // Controlled_Buffer controlled_buffer_6
  assign ALUCtrl = decoder_23_out1 ? 4'b0000 : 4'bz;  // Controlled_Buffer controlled_buffer_7
  assign ALUCtrl = decoder_4_out1 ? 4'b0010 : 4'bz;  // Controlled_Buffer controlled_buffer_8
  assign ALUCtrl = decoder_3_out0 ? 4'b0010 : 4'bz;  // Controlled_Buffer controlled_buffer_9
  assign ALUCtrl = decoder_8_out1 ? 4'b0101 : 4'bz;  // Controlled_Buffer controlled_buffer_10
  Decoder decoder_34 (.en(undriven));  // open: out0, out1, sel
  Decoder decoder_35 ();  // open: out0, out1, sel, en
  Decoder decoder_36 ();  // open: out0, out1, sel, en
  Decoder decoder_37 ();  // open: out0, out1, sel, en
  Decoder decoder_38 ();  // open: out0, out1, sel, en
  Decoder decoder_39 ();  // open: out0, out1, sel, en
  Decoder decoder_40 ();  // open: out0, out1, sel, en
  Decoder decoder_41 ();  // open: out0, out1, sel, en
  Decoder decoder_42 ();  // open: out0, out1, sel, en
  Decoder decoder_43 ();  // open: out0, out1, sel, en
  Decoder decoder_44 ();  // open: out0, out1, sel, en
  Decoder decoder_45 ();  // open: out0, out1, sel, en
  Decoder decoder_46 ();  // open: out0, out1, sel, en
  Decoder decoder_47 ();  // open: out0, out1, sel, en
  Decoder decoder_48 ();  // open: out0, out1, sel, en
  Decoder decoder_49 ();  // open: out0, out1, sel, en
  Decoder decoder_50 ();  // open: out0, out1, sel, en
  Decoder decoder_51 ();  // open: out0, out1, sel, en
  Decoder decoder_52 ();  // open: out0, out1, sel, en
  Decoder decoder_53 ();  // open: out0, out1, sel, en
  Decoder decoder_54 ();  // open: out0, out1, sel, en
  Decoder decoder_55 ();  // open: out0, out1, sel, en
  Decoder decoder_56 ();  // open: out0, out1, sel, en
  Decoder decoder_57 ();  // open: out0, out1, sel, en
  Decoder decoder_58 ();  // open: out0, out1, sel, en
  Decoder decoder_59 ();  // open: out0, out1, sel, en
  Decoder decoder_60 ();  // open: out0, out1, sel, en
  Decoder decoder_61 ();  // open: out0, out1, sel, en
  Decoder decoder_62 ();  // open: out0, out1, sel, en
  Decoder decoder_63 ();  // open: out0, out1, sel, en
  Decoder decoder_64 ();  // open: out0, out1, sel, en
  Decoder decoder_65 ();  // open: out0, out1, sel, en

  // Other names for the same wires on the sheet: lsb = OpCode[0]

  // Notes on the sheet:
  //   Addi
  //   SLTi
  //   ANDi
  //   XOR
  //   Sub
  //   Addi
  //   Addi
  //   Beq
  //   LW
  //   SW
  //   Sub
  //   Sub
  //   Bne
  //   ORi
  //   J
endmodule

// IF/ID
module IF_ID (
  input  [29:0] NPC,
  input  Stage_reset,
  input  [31:0] Instruction,
  input  [5:0] opcode,
  input  Clk,
  output [29:0] NPC1,
  output [31:0] Instruction1,
  output [5:0] OP
);

  Register #(.width(30)) NPC_1 (.D(NPC), .en(1'b1), .clk(Clk), .Q(NPC1), .clr(Stage_reset));
  Register #(.width(32)) Ins (.D(Instruction), .en(1'b1), .clk(Clk), .Q(Instruction1), .clr(Stage_reset));
  Register #(.width(6)) OP_code (.D(opcode), .en(1'b1), .clk(Clk), .Q(OP), .clr(Stage_reset));
endmodule

// ID/Ex
module ID_Ex (
  input  [29:0] NPC1,
  input  [25:0] imm26,
  input  [31:0] busA,
  input  [31:0] busB,
  input  [4:0] Rd1,
  input  Extop_S2,
  input  ALUsrs_S2,
  input  [3:0] ALUctrl_S2,
  input  Beq_S2,
  input  Bne_S2,
  input  J_S2,
  input  MemRead_S2,
  input  MemWrite_S2,
  input  MemToReg_S2,
  input  RegW_S2,
  input  Clk,
  output [29:0] NPC2,
  output [25:0] imm,
  output [31:0] A,
  output [31:0] B,
  output [4:0] Rd2,
  output ExtOp,
  output ALUSrc,
  output [3:0] ALUctrl,
  output Beq,
  output Bne,
  output J,
  output MemRead_S3,
  output MemWrite_S3,
  output MemToReg_S3,
  output RegW_S3
);

  Register #(.width(30)) NPC_2 (.D(NPC1), .en(1'b1), .clk(Clk), .Q(NPC2));  // open: clr
  Register #(.width(26)) immediate (.D(imm26), .en(1'b1), .clk(Clk), .Q(imm));  // open: clr
  Register #(.width(32)) bA (.D(busA), .en(1'b1), .clk(Clk), .Q(A));  // open: clr
  Register #(.width(32)) bB (.D(busB), .en(1'b1), .clk(Clk), .Q(B));  // open: clr
  Register #(.width(5)) Rd_2 (.D(Rd1), .en(1'b1), .clk(Clk), .Q(Rd2));  // open: clr
  Register #(.width(1)) Extender (.D(Extop_S2), .en(1'b1), .clk(Clk), .Q(ExtOp));  // open: clr
  Register #(.width(1)) register_1 (.D(ALUsrs_S2), .en(1'b1), .clk(Clk), .Q(ALUSrc));  // open: clr
  Register #(.width(4)) register_2 (.D(ALUctrl_S2), .en(1'b1), .clk(Clk), .Q(ALUctrl));  // open: clr
  Register #(.width(1)) register_3 (.D(Beq_S2), .en(1'b1), .clk(Clk), .Q(Beq));  // open: clr
  Register #(.width(1)) register_4 (.D(Bne_S2), .en(1'b1), .clk(Clk), .Q(Bne));  // open: clr
  Register #(.width(1)) register_5 (.D(J_S2), .en(1'b1), .clk(Clk), .Q(J));  // open: clr
  Register #(.width(1)) register_6 (.D(MemRead_S2), .en(1'b1), .clk(Clk), .Q(MemRead_S3));  // open: clr
  Register #(.width(1)) register_7 (.D(MemWrite_S2), .en(1'b1), .clk(Clk), .Q(MemWrite_S3));  // open: clr
  Register #(.width(1)) register_8 (.D(MemToReg_S2), .en(1'b1), .clk(Clk), .Q(MemToReg_S3));  // open: clr
  Register #(.width(1)) register_9 (.D(RegW_S2), .en(1'b1), .clk(Clk), .Q(RegW_S3));  // open: clr
endmodule

// Ex/Mem
module Ex_Mem (
  input  [31:0] ALUData,
  input  [31:0] Data,
  input  [4:0] Rd3,
  input  MemRead_S3,
  input  MemWrite_S3,
  input  MemToReg_S3,
  input  RegW_S3,
  input  Clk,
  output [31:0] ALUOut,
  output [31:0] D,
  output [4:0] Rd4,
  output MemRead,
  output MemWrite,
  output MemToReg,
  output RegW_S4
);

  Register #(.width(32)) outP (.D(ALUData), .en(1'b1), .clk(Clk), .Q(ALUOut));  // open: clr
  Register #(.width(32)) Dataa (.D(Data), .en(1'b1), .clk(Clk), .Q(D));  // open: clr
  Register #(.width(5)) Rd_3 (.D(Rd3), .en(1'b1), .clk(Clk), .Q(Rd4));  // open: clr
  Register #(.width(1)) register_1 (.D(MemRead_S3), .en(1'b1), .clk(Clk), .Q(MemRead));  // open: clr
  Register #(.width(1)) register_2 (.D(MemWrite_S3), .en(1'b1), .clk(Clk), .Q(MemWrite));  // open: clr
  Register #(.width(1)) register_3 (.D(MemToReg_S3), .en(1'b1), .clk(Clk), .Q(MemToReg));  // open: clr
  Register #(.width(1)) register_4 (.D(RegW_S3), .en(1'b1), .clk(Clk), .Q(RegW_S4));  // open: clr
endmodule

// Mem/WB
module Mem_WB (
  input  [31:0] Data,
  input  [4:0] Rd3,
  input  RegW_S3,
  input  Clk,
  output [31:0] WBdata,
  output [4:0] Rd4,
  output RegW
);

  Register #(.width(32)) WB_data (.D(Data), .en(1'b1), .clk(Clk), .Q(WBdata));  // open: clr
  Register #(.width(5)) Rd_4 (.D(Rd3), .en(1'b1), .clk(Clk), .Q(Rd4));  // open: clr
  Register #(.width(1)) register_1 (.D(RegW_S3), .en(1'b1), .clk(Clk), .Q(RegW));  // open: clr
endmodule

module Hazard_Control (
  input  [4:0] Rs,
  input  [4:0] Rd2,
  input  [4:0] Rd3,
  input  [4:0] Rd4,
  input  EX_RegWrite,
  input  MEM_RegWrite,
  input  WB_RegWrite,
  input  [4:0] Rt,
  input  MEM_Read,
  output [1:0] ForwardA,
  output [1:0] ForwardB,
  output Stall
);

  wire comparator_1_eq, comparator_2_eq, comparator_3_eq, comparator_4_eq, comparator_5_eq, comparator_6_eq,
       comparator_7_eq, comparator_8_eq, comparator_9_eq, comparator_10_eq, nand_1_out, nand_2_out,
       nand_3_out, nand_4_out, nand_5_out, nand_6_out, not_1_out, not_2_out, or_1_out;
  wire [1:0] multiplexer_1_out, multiplexer_2_out, multiplexer_3_out, multiplexer_4_out, multiplexer_5_out,
       multiplexer_6_out;

  not not_1 (not_1_out, comparator_1_eq);
  Comparator #(.width(5)) comparator_1 (.a(Rs), .b({5{1'b0}}), .eq(comparator_1_eq));  // open: gt, lt
  Comparator #(.width(5)) comparator_2 (.a(Rs), .b(Rd2), .eq(comparator_2_eq));  // open: gt, lt
  Comparator #(.width(5)) comparator_3 (.a(Rs), .b(Rd3), .eq(comparator_3_eq));  // open: gt, lt
  Comparator #(.width(5)) comparator_4 (.a(Rs), .b(Rd4), .eq(comparator_4_eq));  // open: gt, lt
  not not_2 (not_2_out, comparator_5_eq);
  Comparator #(.width(5)) comparator_5 (.a(Rt), .b({5{1'b0}}), .eq(comparator_5_eq));  // open: gt, lt
  Comparator #(.width(5)) comparator_6 (.a(Rt), .b(Rd2), .eq(comparator_6_eq));  // open: gt, lt
  Comparator #(.width(5)) comparator_7 (.a(Rt), .b(Rd3), .eq(comparator_7_eq));  // open: gt, lt
  Comparator #(.width(5)) comparator_8 (.a(Rt), .b(Rd4), .eq(comparator_8_eq));  // open: gt, lt
  nand nand_1 (nand_1_out, comparator_2_eq, EX_RegWrite);
  nand nand_2 (nand_2_out, comparator_3_eq, MEM_RegWrite);
  nand nand_3 (nand_3_out, comparator_4_eq, WB_RegWrite);
  nand nand_4 (nand_4_out, comparator_6_eq, EX_RegWrite);
  nand nand_5 (nand_5_out, comparator_7_eq, MEM_RegWrite);
  nand nand_6 (nand_6_out, comparator_8_eq, WB_RegWrite);
  Multiplexer #(.width(2)) multiplexer_1 (.in0(2'b11), .in1(2'b00), .out(multiplexer_1_out), .sel(nand_3_out));
  Multiplexer #(.width(2)) multiplexer_2 (.in0(2'b11), .in1(2'b00), .out(multiplexer_2_out), .sel(nand_6_out));
  Multiplexer #(.width(2)) multiplexer_3 (
    .in0(2'b10), .in1(multiplexer_1_out), .out(multiplexer_3_out), .sel(nand_2_out));
  Multiplexer #(.width(2)) multiplexer_4 (
    .in0(2'b10), .in1(multiplexer_2_out), .out(multiplexer_4_out), .sel(nand_5_out));
  Comparator #(.width(2)) comparator_9 (.a(2'b01), .b(ForwardA), .eq(comparator_9_eq));  // open: gt, lt
  Comparator #(.width(2)) comparator_10 (.a(ForwardB), .b(2'b01), .eq(comparator_10_eq));  // open: gt, lt
  Multiplexer #(.width(2)) multiplexer_5 (
    .in0(2'b01), .in1(multiplexer_3_out), .out(multiplexer_5_out), .sel(nand_1_out));
  Multiplexer #(.width(2)) multiplexer_6 (
    .in0(2'b01), .in1(multiplexer_4_out), .out(multiplexer_6_out), .sel(nand_4_out));
  or or_1 (or_1_out, comparator_9_eq, comparator_10_eq);
  Multiplexer #(.width(2)) multiplexer_7 (.in0(2'b00), .in1(multiplexer_5_out), .out(ForwardA), .sel(not_1_out));
  Multiplexer #(.width(2)) multiplexer_8 (.in0(2'b00), .in1(multiplexer_6_out), .out(ForwardB), .sel(not_2_out));
  and and_1 (Stall, MEM_Read, or_1_out);

  // Other names for the same wires on the sheet: FA[1:0] = ForwardA; FB[1:0] = ForwardB
endmodule
